// Logisim project comp_proj.circ as structural Verilog: 37 circuits, main circuit main
module main (
);

  wire addcard_1_sign, addcard_1_z, and_2_out, and_3_out, and_4_out, and_5_out, and_6_out, and_7_out,
       clock_1_out, comparator_1_eq, comparator_1_gt, comparator_1_lt, d_ff_1_q, d_ff_2_q, d_ff_3_q,
       d_ff_4_q, nor_1_out, not_2_out, not_3_out_2, not_4_out, not_5_out, or_2_out_3, or_3_out;
  wire [2:0] counter_1_q, register_1_q;
  wire [7:0] addcard_1_r0, adder_1_out, and_1_out, multiplexer_1_out, not_1_out, or_1_out, random_1_out,
       random_2_out, register_2_q, subtractor_1_out, subtractor_2_out, xor_1_out;

  Clock clock_1 (.out(clock_1_out));
  // Probe on random_1_out
  Random random_1 (.clk(clock_1_out), .next(1'b1), .out(random_1_out), .clr(1'b0));
  Random #(.seed(3656)) random_2 (.clk(clock_1_out), .next(1'b1), .out(random_2_out), .clr(1'b0));
  Counter #(.width(3), .max('h7)) counter_1 (
    .load(1'b0), .count(1'b1), .Q(counter_1_q), .clk(clock_1_out), .clr(1'b0));  // open: D, carry
  // Probe on random_2_out
  assign xor_1_out = random_1_out ^ random_2_out;  // XOR_Gate xor_1, 8 bits wide
  assign not_1_out = ~random_1_out;  // NOT_Gate not_1, 8 bits wide
  assign or_1_out = random_1_out | random_2_out;  // OR_Gate or_1, 8 bits wide
  assign and_1_out = random_1_out & random_2_out;  // AND_Gate and_1, 8 bits wide
  Adder adder_1 (.a(random_1_out), .b(random_2_out), .out(adder_1_out));  // open: cin, cout
  Subtractor subtractor_1 (.a(random_1_out), .b(random_2_out), .out(subtractor_1_out));  // open: bin, bout
  addcard addcard_1 (
    .a0(random_1_out[1]), .a1(random_1_out[2]), .a2(random_1_out[3]), .a3(random_1_out[4]),
    .a4(random_1_out[5]), .a5(random_1_out[6]), .a6(random_1_out[7]), .a7(random_2_out[0]),
    .b0(random_2_out[1]), .b1(random_2_out[2]), .b2(random_2_out[3]), .b3(random_2_out[4]),
    .b4(random_2_out[5]), .b5(random_2_out[6]), .b6(random_2_out[7]), .b7(1'b0), .csel(1'b1),
    .clk(clock_1_out), .op0(counter_1_q[0]), .op1(counter_1_q[1]), .op2(counter_1_q[2]),
    .r0(addcard_1_r0[0]), .out_23(addcard_1_r0[1]), .out_24(addcard_1_r0[2]), .out_25(addcard_1_r0[3]),
    .out_26(addcard_1_r0[4]), .out_27(addcard_1_r0[5]), .out_28(addcard_1_r0[6]), .out_29(addcard_1_r0[7]),
    .sign(addcard_1_sign), .z(addcard_1_z));
  Comparator comparator_1 (
    .a(random_1_out), .b(random_2_out), .gt(comparator_1_gt), .eq(comparator_1_eq), .lt(comparator_1_lt));
  Multiplexer #(.select(3), .width(8), .enable("false")) multiplexer_1 (
    .in0(and_1_out), .in1(or_1_out), .in2(not_1_out), .in3(xor_1_out), .in4(adder_1_out),
    .in5(subtractor_1_out), .in6({8{1'b0}}), .in7({8{1'b0}}), .out(multiplexer_1_out), .sel(counter_1_q));
  Subtractor subtractor_2 (.a(multiplexer_1_out), .b(addcard_1_r0), .out(subtractor_2_out));  // open: bin, bout
  Register #(.width(3)) register_1 (.D(counter_1_q), .Q(register_1_q), .clk(clock_1_out));  // open: en, clr
  \or  or_2 (.in_1(addcard_1_sign), .in_2(addcard_1_z), .out_3(or_2_out_3));
  // Probe on multiplexer_1_out
  // Probe on addcard_1_r0
  // Probe on counter_1_q
  and and_2 (and_2_out, register_1_q[0], not_2_out, register_1_q[2], nor_1_out);
  and and_3 (and_3_out, not_4_out, clock_1_out);
  not not_2 (not_2_out, register_1_q[1]);
  \not  not_3 (.in_1(or_2_out_3), .out_2(not_3_out_2));
  // Probe on register_2_q
  // Probe on d_ff_1_q
  Register register_2 (.D(subtractor_2_out), .en(and_4_out), .Q(register_2_q));  // open: clk, clr
  D_Flip_Flop d_ff_1 (.clk(and_3_out), .D(and_2_out), .Q(d_ff_1_q));  // open: Qn, preset, en, reset
  not not_4 (not_4_out, d_ff_1_q);
  D_Flip_Flop d_ff_2 (.clk(clock_1_out), .D(comparator_1_gt), .Q(d_ff_2_q));  // open: Qn, preset, en, reset
  D_Flip_Flop d_ff_3 (.clk(clock_1_out), .D(comparator_1_eq), .Q(d_ff_3_q));  // open: Qn, preset, en, reset
  D_Flip_Flop d_ff_4 (.clk(clock_1_out), .D(comparator_1_lt), .Q(d_ff_4_q));  // open: Qn, preset, en, reset
  and and_4 (and_4_out, not_5_out, clock_1_out);
  or or_3 (or_3_out, register_2_q[0], register_2_q[1], register_2_q[2], register_2_q[3], register_2_q[4], register_2_q[5], register_2_q[6], register_2_q[7]);
  not not_5 (not_5_out, or_3_out);
  and and_5 (and_5_out, d_ff_2_q, not_3_out_2);
  and and_6 (and_6_out, d_ff_3_q, addcard_1_z);
  and and_7 (and_7_out, d_ff_4_q, addcard_1_sign);
  nor nor_1 (nor_1_out, and_5_out, and_6_out, and_7_out);

  // Notes on the sheet:
  //   uut
  //   latched error
endmodule

module op_interpret (
  input  op0,
  input  op1,
  input  op2,
  input  op3,
  output \and ,
  output \or ,
  output \not ,
  output \xor ,
  output add,
  output sub,
  output read,
  output write,
  output mult,
  output div,
  output cmp,
  output jmp,
  output lea,
  output out_18,
  output out_19,
  output out_20
);

  wire nand_1_out, nand_2_out, nand_3_out, nand_4_out, nand_5_out, nand_6_out, nand_7_out, nand_8_out,
       nand_9_out, nand_10_out, nand_11_out, nand_12_out, nand_13_out, nand_14_out, nand_15_out, nand_16_out,
       nand_17_out, nand_18_out, nand_19_out, nand_20_out, nand_21_out, nand_22_out, nand_23_out,
       nand_24_out, nand_25_out, nand_26_out, nand_27_out, nand_28_out, nand_29_out, nand_30_out,
       nand_31_out, nand_32_out, nand_33_out, nand_34_out, nand_35_out, nand_36_out, nand_37_out,
       nand_38_out, nand_39_out, nand_40_out, nand_41_out, nand_42_out, nand_43_out, nand_44_out,
       nand_45_out, nand_46_out, nand_47_out, nand_48_out, nand_49_out, nand_50_out, nand_51_out,
       nand_52_out, nand_53_out, nand_54_out, nand_55_out, nand_56_out, nand_57_out, nand_58_out,
       nand_59_out, nand_60_out, nand_61_out, nand_62_out, nand_63_out, nand_64_out, nand_65_out,
       nand_66_out, nand_67_out, nand_68_out, nand_69_out, nand_70_out, nand_71_out, nand_72_out,
       nand_73_out, nand_74_out, nand_75_out, nand_76_out, nand_77_out, nand_78_out, nand_79_out,
       nand_80_out, nand_81_out, nand_82_out, nand_83_out, nand_84_out;

  nand nand_1 (nand_1_out, op0, op0);
  nand nand_2 (nand_2_out, op1, op1);
  nand nand_3 (nand_3_out, op2, op2);
  nand nand_4 (nand_4_out, op3, op3);
  nand nand_5 (nand_5_out, nand_1_out, nand_2_out);
  nand nand_6 (nand_6_out, nand_3_out, nand_4_out);
  nand nand_7 (nand_7_out, op0, nand_2_out);
  nand nand_8 (nand_8_out, nand_3_out, nand_4_out);
  nand nand_9 (nand_9_out, nand_1_out, op1);
  nand nand_10 (nand_10_out, nand_3_out, nand_4_out);
  nand nand_11 (nand_11_out, op0, op1);
  nand nand_12 (nand_12_out, nand_3_out, nand_4_out);
  nand nand_13 (nand_13_out, nand_1_out, nand_2_out);
  nand nand_14 (nand_14_out, op2, nand_4_out);
  nand nand_15 (nand_15_out, op0, nand_2_out);
  nand nand_16 (nand_16_out, op2, nand_4_out);
  nand nand_17 (nand_17_out, nand_1_out, op1);
  nand nand_18 (nand_18_out, op2, nand_4_out);
  nand nand_19 (nand_19_out, op0, op1);
  nand nand_20 (nand_20_out, op2, nand_4_out);
  nand nand_21 (nand_21_out, nand_1_out, nand_2_out);
  nand nand_22 (nand_22_out, nand_3_out, op3);
  nand nand_23 (nand_23_out, op0, nand_2_out);
  nand nand_24 (nand_24_out, nand_3_out, op3);
  nand nand_25 (nand_25_out, nand_1_out, op1);
  nand nand_26 (nand_26_out, nand_3_out, op3);
  nand nand_27 (nand_27_out, op0, op1);
  nand nand_28 (nand_28_out, nand_3_out, op3);
  nand nand_29 (nand_29_out, nand_1_out, nand_2_out);
  nand nand_30 (nand_30_out, op2, op3);
  nand nand_31 (nand_31_out, op0, nand_2_out);
  nand nand_32 (nand_32_out, op2, op3);
  nand nand_33 (nand_33_out, nand_1_out, op1);
  nand nand_34 (nand_34_out, op2, op3);
  nand nand_35 (nand_35_out, op0, op1);
  nand nand_36 (nand_36_out, op2, op3);
  nand nand_37 (nand_37_out, nand_5_out, nand_5_out);
  nand nand_38 (nand_38_out, nand_6_out, nand_6_out);
  nand nand_39 (nand_39_out, nand_7_out, nand_7_out);
  nand nand_40 (nand_40_out, nand_8_out, nand_8_out);
  nand nand_41 (nand_41_out, nand_9_out, nand_9_out);
  nand nand_42 (nand_42_out, nand_10_out, nand_10_out);
  nand nand_43 (nand_43_out, nand_11_out, nand_11_out);
  nand nand_44 (nand_44_out, nand_12_out, nand_12_out);
  nand nand_45 (nand_45_out, nand_13_out, nand_13_out);
  nand nand_46 (nand_46_out, nand_14_out, nand_14_out);
  nand nand_47 (nand_47_out, nand_15_out, nand_15_out);
  nand nand_48 (nand_48_out, nand_16_out, nand_16_out);
  nand nand_49 (nand_49_out, nand_17_out, nand_17_out);
  nand nand_50 (nand_50_out, nand_18_out, nand_18_out);
  nand nand_51 (nand_51_out, nand_19_out, nand_19_out);
  nand nand_52 (nand_52_out, nand_20_out, nand_20_out);
  nand nand_53 (nand_53_out, nand_21_out, nand_21_out);
  nand nand_54 (nand_54_out, nand_22_out, nand_22_out);
  nand nand_55 (nand_55_out, nand_23_out, nand_23_out);
  nand nand_56 (nand_56_out, nand_24_out, nand_24_out);
  nand nand_57 (nand_57_out, nand_25_out, nand_25_out);
  nand nand_58 (nand_58_out, nand_26_out, nand_26_out);
  nand nand_59 (nand_59_out, nand_27_out, nand_27_out);
  nand nand_60 (nand_60_out, nand_28_out, nand_28_out);
  nand nand_61 (nand_61_out, nand_29_out, nand_29_out);
  nand nand_62 (nand_62_out, nand_30_out, nand_30_out);
  nand nand_63 (nand_63_out, nand_31_out, nand_31_out);
  nand nand_64 (nand_64_out, nand_32_out, nand_32_out);
  nand nand_65 (nand_65_out, nand_33_out, nand_33_out);
  nand nand_66 (nand_66_out, nand_34_out, nand_34_out);
  nand nand_67 (nand_67_out, nand_35_out, nand_35_out);
  nand nand_68 (nand_68_out, nand_36_out, nand_36_out);
  nand nand_69 (nand_69_out, nand_37_out, nand_38_out);
  nand nand_70 (nand_70_out, nand_39_out, nand_40_out);
  nand nand_71 (nand_71_out, nand_41_out, nand_42_out);
  nand nand_72 (nand_72_out, nand_43_out, nand_44_out);
  nand nand_73 (nand_73_out, nand_45_out, nand_46_out);
  nand nand_74 (nand_74_out, nand_47_out, nand_48_out);
  nand nand_75 (nand_75_out, nand_49_out, nand_50_out);
  nand nand_76 (nand_76_out, nand_51_out, nand_52_out);
  nand nand_77 (nand_77_out, nand_53_out, nand_54_out);
  nand nand_78 (nand_78_out, nand_55_out, nand_56_out);
  nand nand_79 (nand_79_out, nand_57_out, nand_58_out);
  nand nand_80 (nand_80_out, nand_59_out, nand_60_out);
  nand nand_81 (nand_81_out, nand_61_out, nand_62_out);
  nand nand_82 (nand_82_out, nand_63_out, nand_64_out);
  nand nand_83 (nand_83_out, nand_65_out, nand_66_out);
  nand nand_84 (nand_84_out, nand_67_out, nand_68_out);
  nand nand_85 (\and , nand_69_out, nand_69_out);
  nand nand_86 (\or , nand_70_out, nand_70_out);
  nand nand_87 (\not , nand_71_out, nand_71_out);
  nand nand_88 (\xor , nand_72_out, nand_72_out);
  nand nand_89 (add, nand_73_out, nand_73_out);
  nand nand_90 (sub, nand_74_out, nand_74_out);
  nand nand_91 (read, nand_75_out, nand_75_out);
  nand nand_92 (write, nand_76_out, nand_76_out);
  nand nand_93 (mult, nand_77_out, nand_77_out);
  nand nand_94 (div, nand_78_out, nand_78_out);
  nand nand_95 (cmp, nand_79_out, nand_79_out);
  nand nand_96 (jmp, nand_80_out, nand_80_out);
  nand nand_97 (lea, nand_81_out, nand_81_out);
  nand nand_98 (out_18, nand_82_out, nand_82_out);
  nand nand_99 (out_19, nand_83_out, nand_83_out);
  nand nand_100 (out_20, nand_84_out, nand_84_out);
endmodule

module \and  (
  input  in_1,
  input  in_2,
  output out_3
);

  wire nand_1_out;

  nand nand_1 (nand_1_out, in_1, in_2);
  nand nand_2 (out_3, nand_1_out, nand_1_out);

  // Notes on the sheet:
  //   in_1: pull=up
endmodule

module \not  (
  input  in_1,
  output out_2
);

  nand nand_1 (out_2, in_1, in_1);
endmodule

module \or  (
  input  in_1,
  input  in_2,
  output out_3
);

  wire nand_1_out, nand_2_out;

  nand nand_1 (nand_1_out, in_1, in_1);
  nand nand_2 (nand_2_out, in_2, in_2);
  nand nand_3 (out_3, nand_1_out, nand_2_out);
endmodule

module \xor  (
  input  in_1,
  input  in_2,
  output out_3
);

  wire nand_1_out, nand_2_out, nand_3_out;

  nand nand_1 (nand_1_out, in_1, in_2);
  nand nand_2 (nand_2_out, in_1, nand_1_out);
  nand nand_3 (nand_3_out, nand_1_out, in_2);
  nand nand_4 (out_3, nand_2_out, nand_3_out);
endmodule

module and8 (
  input  in_1,
  input  in_2,
  input  in_3,
  input  in_4,
  input  in_5,
  input  in_6,
  input  in_7,
  input  in_8,
  input  in_9,
  input  in_10,
  input  in_11,
  input  in_12,
  input  in_13,
  input  in_14,
  input  in_15,
  input  in_16,
  output out_17,
  output out_18,
  output out_19,
  output out_20,
  output out_21,
  output out_22,
  output out_23,
  output out_24
);

  wire nand_1_out, nand_2_out, nand_3_out, nand_4_out, nand_5_out, nand_6_out, nand_7_out, nand_8_out;

  nand nand_1 (nand_1_out, in_1, in_2);
  nand nand_2 (nand_2_out, in_3, in_4);
  nand nand_3 (nand_3_out, in_5, in_6);
  nand nand_4 (nand_4_out, in_7, in_8);
  nand nand_5 (nand_5_out, in_9, in_10);
  nand nand_6 (nand_6_out, in_11, in_12);
  nand nand_7 (nand_7_out, in_13, in_14);
  nand nand_8 (nand_8_out, in_15, in_16);
  nand nand_9 (out_17, nand_1_out, nand_1_out);
  nand nand_10 (out_18, nand_2_out, nand_2_out);
  nand nand_11 (out_19, nand_3_out, nand_3_out);
  nand nand_12 (out_20, nand_4_out, nand_4_out);
  nand nand_13 (out_21, nand_5_out, nand_5_out);
  nand nand_14 (out_22, nand_6_out, nand_6_out);
  nand nand_15 (out_23, nand_7_out, nand_7_out);
  nand nand_16 (out_24, nand_8_out, nand_8_out);
endmodule

module not8 (
  input  in_1,
  input  in_2,
  input  in_3,
  input  in_4,
  input  in_5,
  input  in_6,
  input  in_7,
  input  in_8,
  output out_9,
  output out_10,
  output out_11,
  output out_12,
  output out_13,
  output out_14,
  output out_15,
  output out_16
);

  \not  not_1 (.in_1(in_1), .out_2(out_9));
  \not  not_2 (.in_1(in_2), .out_2(out_10));
  \not  not_3 (.in_1(in_3), .out_2(out_11));
  \not  not_4 (.in_1(in_4), .out_2(out_12));
  \not  not_5 (.in_1(in_5), .out_2(out_13));
  \not  not_6 (.in_1(in_6), .out_2(out_14));
  \not  not_7 (.in_1(in_7), .out_2(out_15));
  \not  not_8 (.in_1(in_8), .out_2(out_16));
endmodule

module or8 (
  input  in_1,
  input  in_2,
  input  in_3,
  input  in_4,
  input  in_5,
  input  in_6,
  input  in_7,
  input  in_8,
  input  in_9,
  input  in_10,
  input  in_11,
  input  in_12,
  input  in_13,
  input  in_14,
  input  in_15,
  input  in_16,
  output out_17,
  output out_18,
  output out_19,
  output out_20,
  output out_21,
  output out_22,
  output out_23,
  output out_24
);

  \or  or_1 (.in_1(in_1), .in_2(in_2), .out_3(out_17));
  \or  or_2 (.in_1(in_3), .in_2(in_4), .out_3(out_18));
  \or  or_3 (.in_1(in_5), .in_2(in_6), .out_3(out_19));
  \or  or_4 (.in_1(in_7), .in_2(in_8), .out_3(out_20));
  \or  or_5 (.in_1(in_9), .in_2(in_10), .out_3(out_21));
  \or  or_6 (.in_1(in_11), .in_2(in_12), .out_3(out_22));
  \or  or_7 (.in_1(in_13), .in_2(in_14), .out_3(out_23));
  \or  or_8 (.in_1(in_15), .in_2(in_16), .out_3(out_24));
endmodule

module xor8 (
  input  in_1,
  input  in_2,
  input  in_3,
  input  in_4,
  input  in_5,
  input  in_6,
  input  in_7,
  input  in_8,
  input  in_9,
  input  in_10,
  input  in_11,
  input  in_12,
  input  in_13,
  input  in_14,
  input  in_15,
  input  in_16,
  output out_17,
  output out_18,
  output out_19,
  output out_20,
  output out_21,
  output out_22,
  output out_23,
  output out_24
);

  \xor  xor_1 (.in_1(in_1), .in_2(in_2), .out_3(out_17));
  \xor  xor_2 (.in_1(in_3), .in_2(in_4), .out_3(out_18));
  \xor  xor_3 (.in_1(in_5), .in_2(in_6), .out_3(out_19));
  \xor  xor_4 (.in_1(in_7), .in_2(in_8), .out_3(out_20));
  \xor  xor_5 (.in_1(in_9), .in_2(in_10), .out_3(out_21));
  \xor  xor_6 (.in_1(in_11), .in_2(in_12), .out_3(out_22));
  \xor  xor_7 (.in_1(in_13), .in_2(in_14), .out_3(out_23));
  \xor  xor_8 (.in_1(in_15), .in_2(in_16), .out_3(out_24));
endmodule

module pfa (
  input  a,
  input  b,
  input  c,
  output g_n,
  output s,
  output p
);

  wire nand_1_out, nand_3_out, nand_4_out;

  nand nand_1 (nand_1_out, a, g_n);
  nand nand_2 (g_n, a, b);
  nand nand_3 (nand_3_out, g_n, b);
  \or  or_1 (.in_1(b), .in_2(a), .out_3(p));
  nand nand_4 (nand_4_out, nand_1_out, nand_3_out);
  \xor  xor_1 (.in_1(nand_4_out), .in_2(c), .out_3(s));
endmodule

module addsub (
  input  sub_sel,
  input  csel,
  input  b7,
  input  b6,
  input  b5,
  input  b4,
  input  b3,
  input  b2,
  input  b1,
  input  b0,
  input  a7,
  input  a6,
  input  a5,
  input  a4,
  input  a3,
  input  a2,
  input  a1,
  input  a0,
  input  cclear,
  input  clk,
  output s7,
  output s6,
  output s5,
  output s4,
  output s3,
  output s2,
  output s1,
  output s0,
  output c7,
  output c8
);

  wire clu8_1_c1, clu8_1_c2, clu8_1_c3, clu8_1_c4, clu8_1_c5, clu8_1_c6, d_ff_1_q, mux21_1_y, nand_1_out,
       pfa_1_g_n, pfa_1_p, pfa_2_g_n, pfa_2_p, pfa_3_g_n, pfa_3_p, pfa_4_g_n, pfa_4_p, pfa_5_g_n, pfa_5_p,
       pfa_6_g_n, pfa_6_p, pfa_7_g_n, pfa_7_p, pfa_8_g_n, pfa_8_p, xor_1_out_3, xor_2_out_3, xor_3_out_3,
       xor_4_out_3, xor_5_out_3, xor_6_out_3, xor_7_out_3, xor_8_out_3;

  pfa pfa_1 (.a(a7), .b(xor_1_out_3), .c(c7), .g_n(pfa_1_g_n), .s(s7), .p(pfa_1_p));
  \xor  xor_1 (.in_1(b7), .in_2(sub_sel), .out_3(xor_1_out_3));
  \xor  xor_2 (.in_1(b6), .in_2(sub_sel), .out_3(xor_2_out_3));
  pfa pfa_2 (.a(a6), .b(xor_2_out_3), .c(clu8_1_c6), .g_n(pfa_2_g_n), .s(s6), .p(pfa_2_p));
  \xor  xor_3 (.in_1(b5), .in_2(sub_sel), .out_3(xor_3_out_3));
  pfa pfa_3 (.a(a5), .b(xor_3_out_3), .c(clu8_1_c5), .g_n(pfa_3_g_n), .s(s5), .p(pfa_3_p));
  \xor  xor_4 (.in_1(b4), .in_2(sub_sel), .out_3(xor_4_out_3));
  pfa pfa_4 (.a(a4), .b(xor_4_out_3), .c(clu8_1_c4), .g_n(pfa_4_g_n), .s(s4), .p(pfa_4_p));
  pfa pfa_5 (.a(a3), .b(xor_5_out_3), .c(clu8_1_c3), .g_n(pfa_5_g_n), .s(s3), .p(pfa_5_p));
  \xor  xor_5 (.in_1(b3), .in_2(sub_sel), .out_3(xor_5_out_3));
  clu8 clu8_1 (
    .c0(mux21_1_y), .p0(pfa_8_p), .g_n0(pfa_8_g_n), .p1(pfa_7_p), .g_n1(pfa_7_g_n), .p2(pfa_6_p),
    .g_n2(pfa_6_g_n), .p3(pfa_5_p), .g_n3(pfa_5_g_n), .p4(pfa_4_p), .g_n4(pfa_4_g_n), .p5(pfa_3_p),
    .g_n5(pfa_3_g_n), .p6(pfa_2_p), .g_n6(pfa_2_g_n), .p7(pfa_1_p), .g_n7(pfa_1_g_n), .c1(clu8_1_c1),
    .c2(clu8_1_c2), .c3(clu8_1_c3), .c4(clu8_1_c4), .c5(clu8_1_c5), .c6(clu8_1_c6), .c7(c7), .c8(c8));
  \xor  xor_6 (.in_1(b2), .in_2(sub_sel), .out_3(xor_6_out_3));
  pfa pfa_6 (.a(a2), .b(xor_6_out_3), .c(clu8_1_c2), .g_n(pfa_6_g_n), .s(s2), .p(pfa_6_p));
  nand nand_1 (nand_1_out, cclear, clk);
  \xor  xor_7 (.in_1(b1), .in_2(sub_sel), .out_3(xor_7_out_3));
  pfa pfa_7 (.a(a1), .b(xor_7_out_3), .c(clu8_1_c1), .g_n(pfa_7_g_n), .s(s1), .p(pfa_7_p));
  D_Flip_Flop d_ff_1 (.clk(nand_1_out), .D(c8), .Q(d_ff_1_q));  // open: Qn, preset, en, reset
  mux21 mux21_1 (.a0(d_ff_1_q), .s(csel), .a0_2(sub_sel), .y(mux21_1_y));
  \xor  xor_8 (.in_1(b0), .in_2(sub_sel), .out_3(xor_8_out_3));
  pfa pfa_8 (.a(a0), .b(xor_8_out_3), .c(mux21_1_y), .g_n(pfa_8_g_n), .s(s0), .p(pfa_8_p));
endmodule

module mux21 (
  input  a0,
  input  s,
  input  a0_2,
  output y
);

  wire nand_1_out, nand_2_out, nand_4_out;

  nand nand_1 (nand_1_out, s, s);
  nand nand_2 (nand_2_out, a0, s);
  nand nand_3 (y, nand_2_out, nand_4_out);
  nand nand_4 (nand_4_out, nand_1_out, a0_2);
endmodule

module clu8 (
  input  c0,
  input  p0,
  input  g_n0,
  input  p1,
  input  g_n1,
  input  p2,
  input  g_n2,
  input  p3,
  input  g_n3,
  input  p4,
  input  g_n4,
  input  p5,
  input  g_n5,
  input  p6,
  input  g_n6,
  input  p7,
  input  g_n7,
  output c1,
  output c2,
  output c3,
  output c4,
  output c5,
  output c6,
  output c7,
  output c8
);

  clublk clublk_1 (.in_1(c0), .in_2(p0), .in_3(g_n0), .out_4(c1));
  clublk clublk_2 (.in_1(c1), .in_2(p1), .in_3(g_n1), .out_4(c2));
  clublk clublk_3 (.in_1(c2), .in_2(p2), .in_3(g_n2), .out_4(c3));
  clublk clublk_4 (.in_1(c3), .in_2(p3), .in_3(g_n3), .out_4(c4));
  clublk clublk_5 (.in_1(c4), .in_2(p4), .in_3(g_n4), .out_4(c5));
  clublk clublk_6 (.in_1(c5), .in_2(p5), .in_3(g_n5), .out_4(c6));
  clublk clublk_7 (.in_1(c6), .in_2(p6), .in_3(g_n6), .out_4(c7));
  clublk clublk_8 (.in_1(c7), .in_2(p7), .in_3(g_n7), .out_4(c8));
endmodule

module clublk (
  input  in_1,
  input  in_2,
  input  in_3,
  output out_4
);

  wire nand_1_out;

  nand nand_1 (nand_1_out, in_1, in_2);
  nand nand_2 (out_4, nand_1_out, in_3);
endmodule

module addcard (
  input  a0,
  input  a1,
  input  a2,
  input  a3,
  input  a4,
  input  a5,
  input  a6,
  input  a7,
  input  b0,
  input  b1,
  input  b2,
  input  b3,
  input  b4,
  input  b5,
  input  b6,
  input  b7,
  input  csel,
  input  clk,
  input  op0,
  input  op1,
  input  op2,
  output r0,
  output out_23,
  output out_24,
  output out_25,
  output out_26,
  output out_27,
  output out_28,
  output out_29,
  output sign,
  output z
);

  wire add_sel_1_compare, add_sel_1_sub_sel, addsub_1_c7, addsub_1_c8, nand_1_out, nand_2_out, nand_3_out;
  wire [5:0] add_sel_1_aop;
  wire [7:0] addsub_1_s0, and8_1_out_17, not8_1_out_9, or8_1_out_17, xor8_1_out_17;

  nand nand_1 (nand_1_out, nand_3_out, nand_3_out);
  nand nand_2 (nand_2_out, add_sel_1_compare, add_sel_1_compare);
  nand nand_3 (nand_3_out, nand_2_out, add_sel_1_aop[4]);
  and8 and8_1 (
    .in_1(a0), .in_2(b0), .in_3(a1), .in_4(b1), .in_5(a2), .in_6(b2), .in_7(a3), .in_8(b3), .in_9(a4),
    .in_10(b4), .in_11(a5), .in_12(b5), .in_13(a6), .in_14(b6), .in_15(a7), .in_16(b7),
    .out_17(and8_1_out_17[0]), .out_18(and8_1_out_17[1]), .out_19(and8_1_out_17[2]),
    .out_20(and8_1_out_17[3]), .out_21(and8_1_out_17[4]), .out_22(and8_1_out_17[5]),
    .out_23(and8_1_out_17[6]), .out_24(and8_1_out_17[7]));
  not8 not8_1 (
    .in_1(a0), .in_2(a1), .in_3(a2), .in_4(a3), .in_5(a4), .in_6(a5), .in_7(a6), .in_8(a7),
    .out_9(not8_1_out_9[0]), .out_10(not8_1_out_9[1]), .out_11(not8_1_out_9[2]), .out_12(not8_1_out_9[3]),
    .out_13(not8_1_out_9[4]), .out_14(not8_1_out_9[5]), .out_15(not8_1_out_9[6]), .out_16(not8_1_out_9[7]));
  or8 or8_1 (
    .in_1(a0), .in_2(b0), .in_3(a1), .in_4(b1), .in_5(a2), .in_6(b2), .in_7(a3), .in_8(b3), .in_9(a4),
    .in_10(b4), .in_11(a5), .in_12(b5), .in_13(a6), .in_14(b6), .in_15(a7), .in_16(b7),
    .out_17(or8_1_out_17[0]), .out_18(or8_1_out_17[1]), .out_19(or8_1_out_17[2]), .out_20(or8_1_out_17[3]),
    .out_21(or8_1_out_17[4]), .out_22(or8_1_out_17[5]), .out_23(or8_1_out_17[6]), .out_24(or8_1_out_17[7]));
  xor8 xor8_1 (
    .in_1(a0), .in_2(b0), .in_3(a1), .in_4(b1), .in_5(a2), .in_6(b2), .in_7(a3), .in_8(b3), .in_9(a4),
    .in_10(b4), .in_11(a5), .in_12(b5), .in_13(a6), .in_14(b6), .in_15(a7), .in_16(b7),
    .out_17(xor8_1_out_17[0]), .out_18(xor8_1_out_17[1]), .out_19(xor8_1_out_17[2]),
    .out_20(xor8_1_out_17[3]), .out_21(xor8_1_out_17[4]), .out_22(xor8_1_out_17[5]),
    .out_23(xor8_1_out_17[6]), .out_24(xor8_1_out_17[7]));
  add_sel add_sel_1 (
    .in_1(op0), .in_2(op1), .in_3(op2), .aop(add_sel_1_aop[0]), .bop(add_sel_1_aop[1]),
    .cop(add_sel_1_aop[2]), .dop(add_sel_1_aop[3]), .eop(add_sel_1_aop[4]), .shift(add_sel_1_aop[5]),
    .compare(add_sel_1_compare), .sub_sel(add_sel_1_sub_sel));
  addsub addsub_1 (
    .b7(b7), .b6(b6), .b5(b5), .b4(b4), .b3(b3), .b2(b2), .b1(b1), .b0(b0), .a7(a7), .a6(a6), .a5(a5),
    .a4(a4), .a3(a3), .a2(a2), .a1(a1), .csel(csel), .a0(a0), .s7(addsub_1_s0[7]), .s6(addsub_1_s0[6]),
    .s5(addsub_1_s0[5]), .s4(addsub_1_s0[4]), .s3(addsub_1_s0[3]), .s2(addsub_1_s0[2]), .s1(addsub_1_s0[1]),
    .s0(addsub_1_s0[0]), .cclear(nand_1_out), .clk(clk), .sub_sel(add_sel_1_sub_sel), .c7(addsub_1_c7),
    .c8(addsub_1_c8));
  compare compare_1 (
    .c7(addsub_1_c7), .c8(addsub_1_c8), .s0(addsub_1_s0[0]), .s1(addsub_1_s0[1]), .s2(addsub_1_s0[2]),
    .s3(addsub_1_s0[3]), .s4(addsub_1_s0[4]), .s5(addsub_1_s0[5]), .s6(addsub_1_s0[6]), .s7(addsub_1_s0[7]),
    .sign(sign), .z(z), .sub_sel(add_sel_1_sub_sel), .clk(clk));
  resmux resmux_1 (
    .in_1(and8_1_out_17), .in_2(or8_1_out_17), .in_3(not8_1_out_9), .in_4(xor8_1_out_17), .in_5(addsub_1_s0),
    .in_6({8{1'b0}}), .in_7(add_sel_1_aop), .out_8(r0), .out_9(out_23), .out_10(out_24), .out_11(out_25),
    .out_12(out_26), .out_13(out_27), .out_14(out_28), .out_15(out_29));
endmodule

module and3 (
  input  in_1,
  input  in_2,
  input  in_3,
  output out_4
);

  wire nand3_1_out_4;

  nand3 nand3_1 (.in_1(in_1), .in_2(in_2), .in_3(in_3), .out_4(nand3_1_out_4));
  \not  not_1 (.in_1(nand3_1_out_4), .out_2(out_4));
endmodule

module add_sel (
  input  in_1,
  input  in_2,
  input  in_3,
  output aop,
  output bop,
  output cop,
  output dop,
  output eop,
  output shift,
  output sub_sel,
  output compare
);

  wire nand3_1_out_4, nand3_2_out_4, not_1_out_2, not_2_out_2, not_3_out_2, not_4_out_2;

  \not  not_1 (.in_1(in_1), .out_2(not_1_out_2));
  \not  not_2 (.in_1(in_2), .out_2(not_2_out_2));
  \not  not_3 (.in_1(in_3), .out_2(not_3_out_2));
  and3 and3_1 (.in_1(not_1_out_2), .in_2(not_2_out_2), .in_3(not_3_out_2), .out_4(aop));
  and3 and3_2 (.in_1(in_1), .in_2(not_2_out_2), .in_3(not_3_out_2), .out_4(bop));
  and3 and3_3 (.in_1(not_1_out_2), .in_2(in_2), .in_3(not_3_out_2), .out_4(cop));
  and3 and3_4 (.in_1(in_1), .in_2(in_2), .in_3(not_3_out_2), .out_4(dop));
  nand3 nand3_1 (.in_1(not_1_out_2), .in_2(not_2_out_2), .in_3(in_3), .out_4(nand3_1_out_4));
  nand3 nand3_2 (.in_1(in_1), .in_2(not_2_out_2), .in_3(in_3), .out_4(nand3_2_out_4));
  and3 and3_5 (.in_1(not_1_out_2), .in_2(in_2), .in_3(in_3), .out_4(shift));
  and3 and3_6 (.in_1(in_1), .in_2(in_2), .in_3(in_3), .out_4(compare));
  nand nand_1 (eop, nand3_1_out_4, nand3_2_out_4);
  \not  not_4 (.in_1(nand3_2_out_4), .out_2(not_4_out_2));
  \or  or_1 (.in_1(not_4_out_2), .in_2(compare), .out_3(sub_sel));
endmodule

module nand3 (
  input  in_1,
  input  in_2,
  input  in_3,
  output out_4
);

  wire nand_1_out, nand_2_out;

  nand nand_1 (nand_1_out, in_1, in_2);
  nand nand_2 (nand_2_out, nand_1_out, nand_1_out);
  nand nand_3 (out_4, nand_2_out, in_3);
endmodule

module compare (
  input  c7,
  input  c8,
  input  sub_sel,
  input  clk,
  input  s0,
  input  s1,
  input  s2,
  input  s3,
  input  s4,
  input  s5,
  input  s6,
  input  s7,
  output sign,
  output z
);

  wire and_1_out_3, and_2_out_3, and_3_out_3, and_4_out_3, not_1_out_2, not_2_out_2, not_3_out_2,
       not_4_out_2, or_1_out_3, or_2_out_3, or_3_out_3, or_4_out_3, xor_1_out_3, xor_2_out_3;

  \xor  xor_1 (.in_1(c7), .in_2(c8), .out_3(xor_1_out_3));
  \and  and_1 (.in_1(sub_sel), .in_2(clk), .out_3(and_1_out_3));
  \or  or_1 (.in_1(s0), .in_2(s1), .out_3(or_1_out_3));
  \or  or_2 (.in_1(s2), .in_2(s3), .out_3(or_2_out_3));
  \or  or_3 (.in_1(s4), .in_2(s5), .out_3(or_3_out_3));
  \or  or_4 (.in_1(s6), .in_2(s7), .out_3(or_4_out_3));
  \xor  xor_2 (.in_1(xor_1_out_3), .in_2(s7), .out_3(xor_2_out_3));
  \not  not_1 (.in_1(or_1_out_3), .out_2(not_1_out_2));
  \not  not_2 (.in_1(or_2_out_3), .out_2(not_2_out_2));
  \not  not_3 (.in_1(or_3_out_3), .out_2(not_3_out_2));
  \not  not_4 (.in_1(or_4_out_3), .out_2(not_4_out_2));
  \and  and_2 (.in_1(not_1_out_2), .in_2(not_2_out_2), .out_3(and_2_out_3));
  \and  and_3 (.in_1(not_3_out_2), .in_2(not_4_out_2), .out_3(and_3_out_3));
  \and  and_4 (.in_1(and_2_out_3), .in_2(and_3_out_3), .out_3(and_4_out_3));
  D_Flip_Flop d_ff_1 (
    .clk(and_1_out_3), .D(xor_2_out_3), .Q(sign), .preset(1'b0), .en(1'b1), .reset(1'b0));  // open: Qn
  D_Flip_Flop d_ff_2 (.clk(and_1_out_3), .D(and_4_out_3), .Q(z), .preset(1'b0), .en(1'b1), .reset(1'b0));  // open: Qn
endmodule

module reg8 (
  input  en,
  input  clk,
  input  in0,
  input  in1,
  input  in2,
  input  in3,
  input  in4,
  input  in5,
  input  in6,
  input  in7,
  output out0,
  output out1,
  output out2,
  output out3,
  output out4,
  output out5,
  output out6,
  output out7
);

  wire nand_1_out, nand_2_out;

  nand nand_1 (nand_1_out, en, clk);
  nand nand_2 (nand_2_out, nand_1_out, nand_1_out);
  D_Flip_Flop d_ff_1 (.clk(nand_2_out), .D(in0), .Q(out0));  // open: Qn, preset, en, reset
  D_Flip_Flop d_ff_2 (.clk(nand_2_out), .D(in1), .Q(out1));  // open: Qn, preset, en, reset
  D_Flip_Flop d_ff_3 (.clk(nand_2_out), .D(in2), .Q(out2));  // open: Qn, preset, en, reset
  D_Flip_Flop d_ff_4 (.clk(nand_2_out), .D(in3), .Q(out3));  // open: Qn, preset, en, reset
  D_Flip_Flop d_ff_5 (.clk(nand_2_out), .D(in4), .Q(out4));  // open: Qn, preset, en, reset
  D_Flip_Flop d_ff_6 (.clk(nand_2_out), .D(in5), .Q(out5));  // open: Qn, preset, en, reset
  D_Flip_Flop d_ff_7 (.clk(nand_2_out), .D(in6), .Q(out6));  // open: Qn, preset, en, reset
  D_Flip_Flop d_ff_8 (.clk(nand_2_out), .D(in7), .Q(out7));  // open: Qn, preset, en, reset
endmodule

module resmuxblk (
  input  \and ,
  input  \or ,
  input  \not ,
  input  \xor ,
  input  sum,
  input  \reg ,
  input  aop,
  input  bop,
  input  cop,
  input  dop,
  input  eop,
  input  fop,
  output res
);

  wire nand_1_out, nand_2_out, nand_3_out, nand_4_out, nand_5_out, nand_6_out, nand_7_out, nand_8_out,
       nand_9_out, nand_10_out, nand_11_out, nand_12_out, nand_13_out, nand_14_out;

  nand nand_1 (nand_1_out, \and , aop);
  nand nand_2 (nand_2_out, \or , bop);
  nand nand_3 (nand_3_out, \not , cop);
  nand nand_4 (nand_4_out, \xor , dop);
  nand nand_5 (nand_5_out, sum, eop);
  nand nand_6 (nand_6_out, \reg , fop);
  nand nand_7 (nand_7_out, nand_1_out, nand_2_out);
  nand nand_8 (nand_8_out, nand_3_out, nand_4_out);
  nand nand_9 (nand_9_out, nand_5_out, nand_6_out);
  nand nand_10 (nand_10_out, nand_7_out, nand_7_out);
  nand nand_11 (nand_11_out, nand_8_out, nand_8_out);
  nand nand_12 (nand_12_out, nand_9_out, nand_9_out);
  nand nand_13 (nand_13_out, nand_14_out, nand_14_out);
  nand nand_14 (nand_14_out, nand_10_out, nand_11_out);
  nand nand_15 (res, nand_13_out, nand_12_out);

  // Notes on the sheet:
  //   reg: pull=down
  //   res: pull=down
endmodule

module resmux (
  input  [7:0] in_1,
  input  [7:0] in_2,
  input  [7:0] in_3,
  input  [7:0] in_4,
  input  [7:0] in_5,
  input  [7:0] in_6,
  input  [5:0] in_7,
  output out_8,
  output out_9,
  output out_10,
  output out_11,
  output out_12,
  output out_13,
  output out_14,
  output out_15
);

  resmuxblk resmuxblk_1 (
    .\and (in_1[0]), .\or (in_2[0]), .\not (in_3[0]), .\xor (in_4[0]), .sum(in_5[0]), .\reg (in_6[0]),
    .aop(in_7[0]), .bop(in_7[1]), .cop(in_7[2]), .dop(in_7[3]), .eop(in_7[4]), .fop(in_7[5]), .res(out_8));
  resmuxblk resmuxblk_2 (
    .\and (in_1[1]), .\or (in_2[1]), .\not (in_3[1]), .\xor (in_4[1]), .sum(in_5[1]), .\reg (in_6[1]),
    .aop(in_7[0]), .bop(in_7[1]), .cop(in_7[2]), .dop(in_7[3]), .eop(in_7[4]), .fop(in_7[5]), .res(out_9));
  resmuxblk resmuxblk_3 (
    .\and (in_1[2]), .\or (in_2[2]), .\not (in_3[2]), .\xor (in_4[2]), .sum(in_5[2]), .\reg (in_6[2]),
    .aop(in_7[0]), .bop(in_7[1]), .cop(in_7[2]), .dop(in_7[3]), .eop(in_7[4]), .fop(in_7[5]), .res(out_10));
  resmuxblk resmuxblk_4 (
    .\and (in_1[3]), .\or (in_2[3]), .\not (in_3[3]), .\xor (in_4[3]), .sum(in_5[3]), .\reg (in_6[3]),
    .aop(in_7[0]), .bop(in_7[1]), .cop(in_7[2]), .dop(in_7[3]), .eop(in_7[4]), .fop(in_7[5]), .res(out_11));
  resmuxblk resmuxblk_5 (
    .\and (in_1[4]), .\or (in_2[4]), .\not (in_3[4]), .\xor (in_4[4]), .sum(in_5[4]), .\reg (in_6[4]),
    .aop(in_7[0]), .bop(in_7[1]), .cop(in_7[2]), .dop(in_7[3]), .eop(in_7[4]), .fop(in_7[5]), .res(out_12));
  resmuxblk resmuxblk_6 (
    .\and (in_1[5]), .\or (in_2[5]), .\not (in_3[5]), .\xor (in_4[5]), .sum(in_5[5]), .\reg (in_6[5]),
    .aop(in_7[0]), .bop(in_7[1]), .cop(in_7[2]), .dop(in_7[3]), .eop(in_7[4]), .fop(in_7[5]), .res(out_13));
  resmuxblk resmuxblk_7 (
    .\and (in_1[6]), .\or (in_2[6]), .\not (in_3[6]), .\xor (in_4[6]), .sum(in_5[6]), .\reg (in_6[6]),
    .aop(in_7[0]), .bop(in_7[1]), .cop(in_7[2]), .dop(in_7[3]), .eop(in_7[4]), .fop(in_7[5]), .res(out_14));
  resmuxblk resmuxblk_8 (
    .\and (in_1[7]), .\or (in_2[7]), .\not (in_3[7]), .\xor (in_4[7]), .sum(in_5[7]), .\reg (in_6[7]),
    .aop(in_7[0]), .bop(in_7[1]), .cop(in_7[2]), .dop(in_7[3]), .eop(in_7[4]), .fop(in_7[5]), .res(out_15));
endmodule

module dff (
  input  clk,
  input  d,
  output q
);

  wire nand_1_out, nand_2_out, nand_3_out, nand_4_out, nand_5_out, nand_6_out, nand_8_out;

  nand nand_1 (nand_1_out, nand_4_out, clk);
  nand nand_2 (nand_2_out, nand_1_out, nand_1_out);
  nand nand_3 (nand_3_out, nand_6_out, nand_4_out);
  nand nand_4 (nand_4_out, nand_3_out, clk);
  nand nand_5 (nand_5_out, nand_2_out, nand_6_out);
  nand nand_6 (nand_6_out, nand_5_out, d);
  nand nand_7 (q, nand_4_out, nand_8_out);
  nand nand_8 (nand_8_out, q, nand_5_out);
endmodule

module mainboard (
);

  wire addcard_1_sign, addcard_1_z, and3_1_out_4, and3_2_out_4, and_1_out_3, and_2_out_3, button_1_out,
       clock_1_out, equality_1_out_7, nand_1_out, nand_2_out, nand_3_out, nand_4_out, nand_5_out, nand_6_out,
       nand_7_out, not_1_out_2, opinterp_1_out_5, opinterp_1_out_6, opinterp_1_out_7, opinterp_1_out_8,
       opinterp_1_out_9, opinterp_1_out_10, opinterp_1_out_11, opinterp_1_out_12, reg_select_1_out_5,
       reg_select_1_out_6, reg_select_1_out_7, reg_select_1_out_8, reg_select_1_out_9, reg_select_1_out_10,
       reg_select_1_out_11, reg_select_1_out_12, reg_select_1_out_13, reg_select_1_out_14,
       reg_select_1_out_15, reg_select_1_out_17, reg_select_1_out_18, reg_select_1_out_19,
       reg_select_1_out_20;
  wire [7:0] addcard_1_r0, multiplier_1_out, multiplier_1_out_2, mux51_1_out_11, mux161_1_out_18,
       mux161_2_out_18, mux218_1_out_25, n16reg_1_out_35, n16reg_1_out_36, n16reg_1_out_37, n16reg_1_out_38,
       n16reg_1_out_39, n16reg_1_out_40, n16reg_1_out_41, n16reg_1_out_42, n16reg_1_out_43, n16reg_1_out_44,
       n16reg_1_out_45, n16reg_1_out_46, n16reg_1_out_47, n16reg_1_out_48, n16reg_1_out_49, n16reg_1_out_50;
  wire [15:0] n16add_1_s0_2, reg_select_2_out_5, reg_select_3_out_5, register_1_q, register_2_q, rom_1_data;

  mux218 mux218_1 (
    .in_1(register_2_q[7]), .in_2(and_1_out_3), .in_3(1'b0), .in_4(register_2_q[6]), .in_5(1'b0),
    .in_6(register_2_q[5]), .in_7(1'b0), .in_8(register_2_q[4]), .in_9(1'b0), .in_10(register_2_q[3]),
    .in_11(1'b0), .in_12(register_2_q[2]), .in_13(1'b0), .in_14(register_2_q[1]), .in_15(1'b0),
    .in_16(register_2_q[0]), .in_17(1'b1), .out_18(mux218_1_out_25[7]), .out_19(mux218_1_out_25[6]),
    .out_20(mux218_1_out_25[5]), .out_21(mux218_1_out_25[4]), .out_22(mux218_1_out_25[3]),
    .out_23(mux218_1_out_25[2]), .out_24(mux218_1_out_25[1]), .out_25(mux218_1_out_25[0]));
  Button button_1 (.out(button_1_out));
  Clock clock_1 (.out(clock_1_out));
  Register #(.width(16)) register_1 (
    .D(n16add_1_s0_2), .Q(register_1_q), .clk(clock_1_out), .clr(button_1_out));  // open: en
  \and  and_1 (.in_1(equality_1_out_7), .in_2(opinterp_1_out_11), .out_3(and_1_out_3));
  _16add u_16add_1 (
    .a7(mux218_1_out_25[7]), .a6(mux218_1_out_25[7]), .a5(mux218_1_out_25[7]), .a4(mux218_1_out_25[7]),
    .a3(mux218_1_out_25[7]), .a2(mux218_1_out_25[7]), .a1(mux218_1_out_25[7]), .a0(mux218_1_out_25[7]),
    .a7_2(mux218_1_out_25[7]), .a6_2(mux218_1_out_25[6]), .a5_2(mux218_1_out_25[5]),
    .a4_2(mux218_1_out_25[4]), .a3_2(mux218_1_out_25[3]), .a2_2(mux218_1_out_25[2]),
    .a1_2(mux218_1_out_25[1]), .a0_2(mux218_1_out_25[0]), .s7(n16add_1_s0_2[15]), .s6(n16add_1_s0_2[14]),
    .s5(n16add_1_s0_2[13]), .s4(n16add_1_s0_2[12]), .s3(n16add_1_s0_2[11]), .s2(n16add_1_s0_2[10]),
    .s1(n16add_1_s0_2[9]), .s0(n16add_1_s0_2[8]), .s7_2(n16add_1_s0_2[7]), .s6_2(n16add_1_s0_2[6]),
    .s5_2(n16add_1_s0_2[5]), .s4_2(n16add_1_s0_2[4]), .s3_2(n16add_1_s0_2[3]), .s2_2(n16add_1_s0_2[2]),
    .s1_2(n16add_1_s0_2[1]), .s0_2(n16add_1_s0_2[0]), .b7(register_1_q[15]), .b6(register_1_q[14]),
    .b5(register_1_q[13]), .b4(register_1_q[12]), .b3(register_1_q[11]), .b2(register_1_q[10]),
    .b1(register_1_q[9]), .b0(register_1_q[8]), .b7_2(register_1_q[7]), .b6_2(register_1_q[6]),
    .b5_2(register_1_q[5]), .b4_2(register_1_q[4]), .b3_2(register_1_q[3]), .b2_2(register_1_q[2]),
    .b1_2(register_1_q[1]), .b0_2(register_1_q[0]));
  equality equality_1 (
    .in_1(addcard_1_sign), .in_2(addcard_1_z), .in_3(register_2_q[11]), .in_4(register_2_q[10]),
    .in_5(register_2_q[9]), .in_6(register_2_q[8]), .out_7(equality_1_out_7));
  ROM #(.addrWidth(16), .dataWidth(16)) rom_1 (.addr(register_1_q), .data(rom_1_data));  // open: sel
  // Probe on register_2_q
  Register #(.width(16)) register_2 (
    .D(rom_1_data), .Q(register_2_q), .clk(clock_1_out), .clr(button_1_out));  // open: en
  reg_select reg_select_1 (
    .in_1(register_2_q[11]), .in_2(register_2_q[10]), .in_3(register_2_q[9]), .in_4(register_2_q[8]),
    .out_5(reg_select_1_out_5), .out_6(reg_select_1_out_6), .out_7(reg_select_1_out_7),
    .out_8(reg_select_1_out_8), .out_9(reg_select_1_out_9), .out_10(reg_select_1_out_10),
    .out_11(reg_select_1_out_11), .out_12(reg_select_1_out_12), .out_13(reg_select_1_out_13),
    .out_14(reg_select_1_out_14), .out_15(reg_select_1_out_15), .out_17(reg_select_1_out_17),
    .out_18(reg_select_1_out_18), .out_19(reg_select_1_out_19), .out_20(reg_select_1_out_20));  // open: out_16
  reg_select reg_select_2 (
    .in_1(register_2_q[7]), .in_2(register_2_q[6]), .in_3(register_2_q[5]), .in_4(register_2_q[4]),
    .out_5(reg_select_2_out_5[0]), .out_6(reg_select_2_out_5[1]), .out_7(reg_select_2_out_5[2]),
    .out_8(reg_select_2_out_5[3]), .out_9(reg_select_2_out_5[4]), .out_10(reg_select_2_out_5[5]),
    .out_11(reg_select_2_out_5[6]), .out_12(reg_select_2_out_5[7]), .out_13(reg_select_2_out_5[8]),
    .out_14(reg_select_2_out_5[9]), .out_15(reg_select_2_out_5[10]), .out_16(reg_select_2_out_5[11]),
    .out_17(reg_select_2_out_5[12]), .out_18(reg_select_2_out_5[13]), .out_19(reg_select_2_out_5[14]),
    .out_20(reg_select_2_out_5[15]));
  reg_select reg_select_3 (
    .in_1(register_2_q[3]), .in_2(register_2_q[2]), .in_3(register_2_q[1]), .in_4(register_2_q[0]),
    .out_5(reg_select_3_out_5[0]), .out_6(reg_select_3_out_5[1]), .out_7(reg_select_3_out_5[2]),
    .out_8(reg_select_3_out_5[3]), .out_9(reg_select_3_out_5[4]), .out_10(reg_select_3_out_5[5]),
    .out_11(reg_select_3_out_5[6]), .out_12(reg_select_3_out_5[7]), .out_13(reg_select_3_out_5[8]),
    .out_14(reg_select_3_out_5[9]), .out_15(reg_select_3_out_5[10]), .out_16(reg_select_3_out_5[11]),
    .out_17(reg_select_3_out_5[12]), .out_18(reg_select_3_out_5[13]), .out_19(reg_select_3_out_5[14]),
    .out_20(reg_select_3_out_5[15]));
  // Probe on mux51_1_out_11
  mux51 mux51_1 (
    .in_2(addcard_1_r0), .in_3({8{1'b0}}), .in_4(multiplier_1_out),
    .in_5({register_2_q[0], register_2_q[1], register_2_q[2], register_2_q[3], register_2_q[4], register_2_q[5], register_2_q[6], register_2_q[7]}),
    .out_11(mux51_1_out_11), .in_6(opinterp_1_out_7), .in_7(nand_1_out), .in_8(opinterp_1_out_6),
    .in_9(opinterp_1_out_5), .in_10(opinterp_1_out_12));  // open: in_1
  // Probe on n16reg_1_out_35
  // Probe on n16reg_1_out_37
  // Probe on n16reg_1_out_39
  // Probe on n16reg_1_out_40
  // Probe on n16reg_1_out_38
  // Probe on n16reg_1_out_36
  _16reg u_16reg_1 (
    .in_3(mux51_1_out_11), .in_4(reg_select_1_out_6), .in_5(mux51_1_out_11), .in_6(reg_select_1_out_7),
    .in_7(mux51_1_out_11), .in_8(reg_select_1_out_8), .in_9(mux51_1_out_11), .in_10(reg_select_1_out_9),
    .in_11(mux51_1_out_11), .in_12(reg_select_1_out_10), .in_13(mux51_1_out_11), .in_14(reg_select_1_out_11),
    .in_15(mux51_1_out_11), .in_16(reg_select_1_out_12), .in_17(mux51_1_out_11), .in_18(reg_select_1_out_13),
    .in_19(mux51_1_out_11), .in_20(reg_select_1_out_14), .in_21(mux51_1_out_11), .in_22(reg_select_1_out_15),
    .in_23(multiplier_1_out_2), .in_24(opinterp_1_out_5), .in_25(mux51_1_out_11),
    .in_26(reg_select_1_out_17), .in_27(mux51_1_out_11), .in_28(reg_select_1_out_18), .in_29(mux51_1_out_11),
    .in_30(reg_select_1_out_19), .in_31(mux51_1_out_11), .in_32(reg_select_1_out_20), .in_33(and_2_out_3),
    .out_36(n16reg_1_out_36), .out_37(n16reg_1_out_37), .out_38(n16reg_1_out_38), .out_39(n16reg_1_out_39),
    .out_40(n16reg_1_out_40), .out_41(n16reg_1_out_41), .out_42(n16reg_1_out_42), .out_43(n16reg_1_out_43),
    .out_44(n16reg_1_out_44), .out_45(n16reg_1_out_45), .out_46(n16reg_1_out_46), .out_47(n16reg_1_out_47),
    .out_48(n16reg_1_out_48), .out_49(n16reg_1_out_49), .out_50(n16reg_1_out_50), .in_34(button_1_out),
    .in_1(mux51_1_out_11), .out_35(n16reg_1_out_35), .in_2(reg_select_1_out_5));
  // Probe on n16reg_1_out_43
  // Probe on n16reg_1_out_41
  // Probe on n16reg_1_out_45
  // Probe on n16reg_1_out_44
  // Probe on n16reg_1_out_46
  // Probe on n16reg_1_out_42
  nand nand_1 (nand_1_out, register_2_q[15], register_2_q[15]);
  // Probe on n16reg_1_out_47
  // Probe on n16reg_1_out_49
  // Probe on n16reg_1_out_48
  // Probe on n16reg_1_out_50
  mux161 mux161_1 (
    .in_1(reg_select_2_out_5), .in_3(n16reg_1_out_36), .in_4(n16reg_1_out_37), .in_5(n16reg_1_out_38),
    .in_6(n16reg_1_out_39), .in_7(n16reg_1_out_40), .in_8(n16reg_1_out_41), .in_9(n16reg_1_out_42),
    .in_10(n16reg_1_out_43), .in_11(n16reg_1_out_44), .in_12(n16reg_1_out_45), .in_13(n16reg_1_out_46),
    .in_14(n16reg_1_out_47), .in_15(n16reg_1_out_48), .in_16(n16reg_1_out_49), .in_17(n16reg_1_out_50),
    .out_18(mux161_1_out_18), .in_2(n16reg_1_out_35));
  mux161 mux161_2 (
    .in_1(reg_select_3_out_5), .in_3(n16reg_1_out_36), .in_4(n16reg_1_out_37), .in_5(n16reg_1_out_38),
    .in_6(n16reg_1_out_39), .in_7(n16reg_1_out_40), .in_8(n16reg_1_out_41), .in_9(n16reg_1_out_42),
    .in_10(n16reg_1_out_43), .in_11(n16reg_1_out_44), .in_12(n16reg_1_out_45), .in_13(n16reg_1_out_46),
    .in_14(n16reg_1_out_47), .in_15(n16reg_1_out_48), .in_16(n16reg_1_out_49), .in_17(n16reg_1_out_50),
    .out_18(mux161_2_out_18), .in_2(n16reg_1_out_35));
  \and  and_2 (.in_1(clock_1_out), .in_2(and3_1_out_4), .out_3(and_2_out_3));
  // Probe on mux161_1_out_18
  // Probe on mux161_2_out_18
  and3 and3_1 (.in_1(nand_4_out), .in_2(nand_3_out), .in_3(nand_2_out), .out_4(and3_1_out_4));
  opinterp opinterp_1 (
    .in_1(register_2_q[12]), .in_2(register_2_q[13]), .in_3(register_2_q[14]), .in_4(register_2_q[15]),
    .out_5(opinterp_1_out_5), .out_6(opinterp_1_out_6), .out_7(opinterp_1_out_7), .out_8(opinterp_1_out_8),
    .out_9(opinterp_1_out_9), .out_10(opinterp_1_out_10), .out_11(opinterp_1_out_11),
    .out_12(opinterp_1_out_12));
  nand nand_2 (nand_2_out, opinterp_1_out_11, opinterp_1_out_11);
  nand nand_3 (nand_3_out, opinterp_1_out_8, opinterp_1_out_8);
  nand nand_4 (nand_4_out, not_1_out_2, and3_2_out_4);
  \not  not_1 (.in_1(register_2_q[15]), .out_2(not_1_out_2));
  Multiplier #(.width(16)) multiplier_1 (
    .a({{8{1'b0}}, mux161_1_out_18}), .b({{8{1'b0}}, mux161_2_out_18}),
    .out({multiplier_1_out_2, multiplier_1_out}));  // open: cin, cout
  and3 and3_2 (.in_1(register_2_q[12]), .in_2(register_2_q[13]), .in_3(register_2_q[14]), .out_4(and3_2_out_4));
  nand nand_5 (nand_5_out, opinterp_1_out_9, opinterp_1_out_9);
  nand nand_6 (nand_6_out, opinterp_1_out_10, opinterp_1_out_10);
  nand nand_7 (nand_7_out, nand_5_out, nand_6_out);
  addcard addcard_1 (
    .a0(mux161_1_out_18[0]), .a1(mux161_1_out_18[1]), .a2(mux161_1_out_18[2]), .a3(mux161_1_out_18[3]),
    .a4(mux161_1_out_18[4]), .a5(mux161_1_out_18[5]), .a6(mux161_1_out_18[6]), .a7(mux161_1_out_18[7]),
    .b0(mux161_2_out_18[0]), .b1(mux161_2_out_18[1]), .b2(mux161_2_out_18[2]), .b3(mux161_2_out_18[3]),
    .b4(mux161_2_out_18[4]), .b5(mux161_2_out_18[5]), .b6(mux161_2_out_18[6]), .b7(mux161_2_out_18[7]),
    .csel(nand_7_out), .clk(clock_1_out), .op0(register_2_q[12]), .op1(register_2_q[13]),
    .op2(register_2_q[14]), .r0(addcard_1_r0[0]), .out_23(addcard_1_r0[1]), .out_24(addcard_1_r0[2]),
    .out_25(addcard_1_r0[3]), .out_26(addcard_1_r0[4]), .out_27(addcard_1_r0[5]), .out_28(addcard_1_r0[6]),
    .out_29(addcard_1_r0[7]), .sign(addcard_1_sign), .z(addcard_1_z));

  // Notes on the sheet:
  //   contents of rom_1 (hex, n*v repeats v):
  //   f2aa f102 4021 0 b001 b012 a200 7011 8401 e0fb
endmodule

module reg_select (
  input  in_1,
  input  in_2,
  input  in_3,
  input  in_4,
  output out_5,
  output out_6,
  output out_7,
  output out_8,
  output out_9,
  output out_10,
  output out_11,
  output out_12,
  output out_13,
  output out_14,
  output out_15,
  output out_16,
  output out_17,
  output out_18,
  output out_19,
  output out_20
);

  wire nand_1_out, nand_2_out, nand_3_out, nand_4_out, nand_5_out, nand_6_out, nand_7_out, nand_8_out,
       nand_9_out, nand_10_out, nand_11_out, nand_12_out, nand_13_out, nand_14_out, nand_15_out, nand_16_out,
       nand_17_out, nand_18_out, nand_19_out, nand_20_out, nand_21_out, nand_22_out, nand_23_out,
       nand_24_out, nand_25_out, nand_26_out, nand_27_out, nand_28_out, nand_29_out, nand_30_out,
       nand_31_out, nand_32_out, nand_33_out, nand_34_out, nand_35_out, nand_36_out, nand_37_out,
       nand_38_out, nand_39_out, nand_40_out, nand_41_out, nand_42_out, nand_43_out, nand_44_out,
       nand_45_out, nand_46_out, nand_47_out, nand_48_out, nand_49_out, nand_50_out, nand_51_out,
       nand_52_out, nand_53_out, nand_54_out, nand_55_out, nand_56_out, nand_57_out, nand_58_out,
       nand_59_out, nand_60_out, nand_61_out, nand_62_out, nand_63_out, nand_64_out, nand_65_out,
       nand_66_out, nand_67_out, nand_68_out, nand_69_out, nand_70_out, nand_71_out, nand_72_out,
       nand_73_out, nand_74_out, nand_75_out, nand_76_out, nand_77_out, nand_78_out, nand_79_out,
       nand_80_out, nand_81_out, nand_82_out, nand_83_out, nand_84_out;

  nand nand_1 (nand_1_out, in_4, in_4);
  nand nand_2 (nand_2_out, in_3, in_3);
  nand nand_3 (nand_3_out, in_2, in_2);
  nand nand_4 (nand_4_out, in_1, in_1);
  nand nand_5 (nand_5_out, nand_1_out, nand_2_out);
  nand nand_6 (nand_6_out, nand_3_out, nand_4_out);
  nand nand_7 (nand_7_out, in_4, nand_2_out);
  nand nand_8 (nand_8_out, nand_3_out, nand_4_out);
  nand nand_9 (nand_9_out, nand_1_out, in_3);
  nand nand_10 (nand_10_out, nand_3_out, nand_4_out);
  nand nand_11 (nand_11_out, in_4, in_3);
  nand nand_12 (nand_12_out, nand_3_out, nand_4_out);
  nand nand_13 (nand_13_out, nand_1_out, nand_2_out);
  nand nand_14 (nand_14_out, in_2, nand_4_out);
  nand nand_15 (nand_15_out, in_4, nand_2_out);
  nand nand_16 (nand_16_out, in_2, nand_4_out);
  nand nand_17 (nand_17_out, nand_1_out, in_3);
  nand nand_18 (nand_18_out, in_2, nand_4_out);
  nand nand_19 (nand_19_out, in_4, in_3);
  nand nand_20 (nand_20_out, in_2, nand_4_out);
  nand nand_21 (nand_21_out, nand_1_out, nand_2_out);
  nand nand_22 (nand_22_out, nand_3_out, in_1);
  nand nand_23 (nand_23_out, in_4, nand_2_out);
  nand nand_24 (nand_24_out, nand_3_out, in_1);
  nand nand_25 (nand_25_out, nand_1_out, in_3);
  nand nand_26 (nand_26_out, nand_3_out, in_1);
  nand nand_27 (nand_27_out, in_4, in_3);
  nand nand_28 (nand_28_out, nand_3_out, in_1);
  nand nand_29 (nand_29_out, nand_1_out, nand_2_out);
  nand nand_30 (nand_30_out, in_2, in_1);
  nand nand_31 (nand_31_out, in_4, nand_2_out);
  nand nand_32 (nand_32_out, in_2, in_1);
  nand nand_33 (nand_33_out, nand_1_out, in_3);
  nand nand_34 (nand_34_out, in_2, in_1);
  nand nand_35 (nand_35_out, in_4, in_3);
  nand nand_36 (nand_36_out, in_2, in_1);
  nand nand_37 (nand_37_out, nand_5_out, nand_5_out);
  nand nand_38 (nand_38_out, nand_6_out, nand_6_out);
  nand nand_39 (nand_39_out, nand_7_out, nand_7_out);
  nand nand_40 (nand_40_out, nand_8_out, nand_8_out);
  nand nand_41 (nand_41_out, nand_9_out, nand_9_out);
  nand nand_42 (nand_42_out, nand_10_out, nand_10_out);
  nand nand_43 (nand_43_out, nand_11_out, nand_11_out);
  nand nand_44 (nand_44_out, nand_12_out, nand_12_out);
  nand nand_45 (nand_45_out, nand_13_out, nand_13_out);
  nand nand_46 (nand_46_out, nand_14_out, nand_14_out);
  nand nand_47 (nand_47_out, nand_15_out, nand_15_out);
  nand nand_48 (nand_48_out, nand_16_out, nand_16_out);
  nand nand_49 (nand_49_out, nand_17_out, nand_17_out);
  nand nand_50 (nand_50_out, nand_18_out, nand_18_out);
  nand nand_51 (nand_51_out, nand_19_out, nand_19_out);
  nand nand_52 (nand_52_out, nand_20_out, nand_20_out);
  nand nand_53 (nand_53_out, nand_21_out, nand_21_out);
  nand nand_54 (nand_54_out, nand_22_out, nand_22_out);
  nand nand_55 (nand_55_out, nand_23_out, nand_23_out);
  nand nand_56 (nand_56_out, nand_24_out, nand_24_out);
  nand nand_57 (nand_57_out, nand_25_out, nand_25_out);
  nand nand_58 (nand_58_out, nand_26_out, nand_26_out);
  nand nand_59 (nand_59_out, nand_27_out, nand_27_out);
  nand nand_60 (nand_60_out, nand_28_out, nand_28_out);
  nand nand_61 (nand_61_out, nand_29_out, nand_29_out);
  nand nand_62 (nand_62_out, nand_30_out, nand_30_out);
  nand nand_63 (nand_63_out, nand_31_out, nand_31_out);
  nand nand_64 (nand_64_out, nand_32_out, nand_32_out);
  nand nand_65 (nand_65_out, nand_33_out, nand_33_out);
  nand nand_66 (nand_66_out, nand_34_out, nand_34_out);
  nand nand_67 (nand_67_out, nand_35_out, nand_35_out);
  nand nand_68 (nand_68_out, nand_36_out, nand_36_out);
  nand nand_69 (nand_69_out, nand_37_out, nand_38_out);
  nand nand_70 (nand_70_out, nand_39_out, nand_40_out);
  nand nand_71 (nand_71_out, nand_41_out, nand_42_out);
  nand nand_72 (nand_72_out, nand_43_out, nand_44_out);
  nand nand_73 (nand_73_out, nand_45_out, nand_46_out);
  nand nand_74 (nand_74_out, nand_47_out, nand_48_out);
  nand nand_75 (nand_75_out, nand_49_out, nand_50_out);
  nand nand_76 (nand_76_out, nand_51_out, nand_52_out);
  nand nand_77 (nand_77_out, nand_53_out, nand_54_out);
  nand nand_78 (nand_78_out, nand_55_out, nand_56_out);
  nand nand_79 (nand_79_out, nand_57_out, nand_58_out);
  nand nand_80 (nand_80_out, nand_59_out, nand_60_out);
  nand nand_81 (nand_81_out, nand_61_out, nand_62_out);
  nand nand_82 (nand_82_out, nand_63_out, nand_64_out);
  nand nand_83 (nand_83_out, nand_65_out, nand_66_out);
  nand nand_84 (nand_84_out, nand_67_out, nand_68_out);
  nand nand_85 (out_5, nand_69_out, nand_69_out);
  nand nand_86 (out_6, nand_70_out, nand_70_out);
  nand nand_87 (out_7, nand_71_out, nand_71_out);
  nand nand_88 (out_8, nand_72_out, nand_72_out);
  nand nand_89 (out_9, nand_73_out, nand_73_out);
  nand nand_90 (out_10, nand_74_out, nand_74_out);
  nand nand_91 (out_11, nand_75_out, nand_75_out);
  nand nand_92 (out_12, nand_76_out, nand_76_out);
  nand nand_93 (out_13, nand_77_out, nand_77_out);
  nand nand_94 (out_14, nand_78_out, nand_78_out);
  nand nand_95 (out_15, nand_79_out, nand_79_out);
  nand nand_96 (out_16, nand_80_out, nand_80_out);
  nand nand_97 (out_17, nand_81_out, nand_81_out);
  nand nand_98 (out_18, nand_82_out, nand_82_out);
  nand nand_99 (out_19, nand_83_out, nand_83_out);
  nand nand_100 (out_20, nand_84_out, nand_84_out);

  // Notes on the sheet:
  //   NOT IN REG WRITE
endmodule

module _16reg (
  input  [7:0] in_1,
  input  in_2,
  input  [7:0] in_3,
  input  in_4,
  input  [7:0] in_5,
  input  in_6,
  input  [7:0] in_7,
  input  in_8,
  input  [7:0] in_9,
  input  in_10,
  input  [7:0] in_11,
  input  in_12,
  input  [7:0] in_13,
  input  in_14,
  input  [7:0] in_15,
  input  in_16,
  input  [7:0] in_17,
  input  in_18,
  input  [7:0] in_19,
  input  in_20,
  input  [7:0] in_21,
  input  in_22,
  input  [7:0] in_23,
  input  in_24,
  input  [7:0] in_25,
  input  in_26,
  input  [7:0] in_27,
  input  in_28,
  input  [7:0] in_29,
  input  in_30,
  input  [7:0] in_31,
  input  in_32,
  input  in_33,
  input  in_34,
  output [7:0] out_35,
  output [7:0] out_36,
  output [7:0] out_37,
  output [7:0] out_38,
  output [7:0] out_39,
  output [7:0] out_40,
  output [7:0] out_41,
  output [7:0] out_42,
  output [7:0] out_43,
  output [7:0] out_44,
  output [7:0] out_45,
  output [7:0] out_46,
  output [7:0] out_47,
  output [7:0] out_48,
  output [7:0] out_49,
  output [7:0] out_50
);

  Register register_1 (.D(in_1), .en(in_2), .Q(out_35), .clk(in_33), .clr(in_34));
  Register register_2 (.D(in_3), .en(in_4), .Q(out_36), .clk(in_33), .clr(in_34));
  Register register_3 (.D(in_5), .en(in_6), .Q(out_37), .clk(in_33), .clr(in_34));
  Register register_4 (.D(in_7), .en(in_8), .Q(out_38), .clk(in_33), .clr(in_34));
  Register register_5 (.D(in_9), .en(in_10), .Q(out_39), .clk(in_33), .clr(in_34));
  Register register_6 (.D(in_11), .en(in_12), .Q(out_40), .clk(in_33), .clr(in_34));
  Register register_7 (.D(in_13), .en(in_14), .Q(out_41), .clk(in_33), .clr(in_34));
  Register register_8 (.D(in_15), .en(in_16), .Q(out_42), .clk(in_33), .clr(in_34));
  Register register_9 (.D(in_17), .en(in_18), .Q(out_43), .clk(in_33), .clr(in_34));
  Register register_10 (.D(in_19), .en(in_20), .Q(out_44), .clk(in_33), .clr(in_34));
  Register register_11 (.D(in_21), .en(in_22), .Q(out_45), .clk(in_33), .clr(in_34));
  Register register_12 (.D(in_23), .en(in_24), .Q(out_46), .clk(in_33), .clr(in_34));
  Register register_13 (.D(in_25), .en(in_26), .Q(out_47), .clk(in_33), .clr(in_34));
  Register register_14 (.D(in_27), .en(in_28), .Q(out_48), .clk(in_33), .clr(in_34));
  Register register_15 (.D(in_29), .en(in_30), .Q(out_49), .clk(in_33), .clr(in_34));
  Register register_16 (.D(in_31), .en(in_32), .Q(out_50), .clk(in_33), .clr(in_34));
endmodule

module mux161blk (
  input  in_1,
  input  in_2,
  input  in_3,
  input  in_4,
  input  in_5,
  input  in_6,
  input  in_7,
  input  in_8,
  input  in_9,
  input  in_10,
  input  in_11,
  input  in_12,
  input  in_13,
  input  in_14,
  input  in_15,
  input  in_16,
  input  in_17,
  input  in_18,
  input  in_19,
  input  in_20,
  input  in_21,
  input  in_22,
  input  in_23,
  input  in_24,
  input  in_25,
  input  in_26,
  input  in_27,
  input  in_28,
  input  in_29,
  input  in_30,
  input  in_31,
  input  in_32,
  output out_33
);

  wire and_1_out_3, and_2_out_3, and_3_out_3, and_4_out_3, and_5_out_3, and_6_out_3, and_7_out_3,
       and_8_out_3, and_9_out_3, and_10_out_3, and_11_out_3, and_12_out_3, and_13_out_3, and_14_out_3,
       and_15_out_3, nand_1_out, nand_2_out, nand_3_out, nand_4_out, nand_5_out, nand_6_out, nand_7_out,
       nand_8_out, nand_9_out, nand_10_out, nand_11_out, nand_12_out, nand_13_out, nand_14_out, nand_15_out,
       nand_16_out;

  nand nand_1 (nand_1_out, in_1, in_2);
  nand nand_2 (nand_2_out, in_3, in_4);
  nand nand_3 (nand_3_out, in_5, in_6);
  nand nand_4 (nand_4_out, in_7, in_8);
  nand nand_5 (nand_5_out, in_9, in_10);
  nand nand_6 (nand_6_out, in_11, in_12);
  nand nand_7 (nand_7_out, in_13, in_14);
  nand nand_8 (nand_8_out, in_15, in_16);
  nand nand_9 (nand_9_out, in_17, in_18);
  nand nand_10 (nand_10_out, in_19, in_20);
  nand nand_11 (nand_11_out, in_21, in_22);
  nand nand_12 (nand_12_out, in_23, in_24);
  nand nand_13 (nand_13_out, in_25, in_26);
  nand nand_14 (nand_14_out, in_27, in_28);
  nand nand_15 (nand_15_out, in_29, in_30);
  nand nand_16 (nand_16_out, in_31, in_32);
  \and  and_1 (.in_1(nand_1_out), .in_2(nand_2_out), .out_3(and_1_out_3));
  \and  and_2 (.in_1(nand_3_out), .in_2(nand_4_out), .out_3(and_2_out_3));
  \and  and_3 (.in_1(nand_5_out), .in_2(nand_6_out), .out_3(and_3_out_3));
  \and  and_4 (.in_1(nand_7_out), .in_2(nand_8_out), .out_3(and_4_out_3));
  \and  and_5 (.in_1(nand_9_out), .in_2(nand_10_out), .out_3(and_5_out_3));
  \and  and_6 (.in_1(nand_11_out), .in_2(nand_12_out), .out_3(and_6_out_3));
  \and  and_7 (.in_1(nand_13_out), .in_2(nand_14_out), .out_3(and_7_out_3));
  \and  and_8 (.in_1(nand_15_out), .in_2(nand_16_out), .out_3(and_8_out_3));
  \and  and_9 (.in_1(and_1_out_3), .in_2(and_2_out_3), .out_3(and_9_out_3));
  \and  and_10 (.in_1(and_3_out_3), .in_2(and_4_out_3), .out_3(and_10_out_3));
  \and  and_11 (.in_1(and_5_out_3), .in_2(and_6_out_3), .out_3(and_11_out_3));
  \and  and_12 (.in_1(and_7_out_3), .in_2(and_8_out_3), .out_3(and_12_out_3));
  \and  and_13 (.in_1(and_9_out_3), .in_2(and_10_out_3), .out_3(and_13_out_3));
  \and  and_14 (.in_1(and_11_out_3), .in_2(and_12_out_3), .out_3(and_14_out_3));
  \and  and_15 (.in_1(and_13_out_3), .in_2(and_14_out_3), .out_3(and_15_out_3));
  \not  not_1 (.in_1(and_15_out_3), .out_2(out_33));
endmodule

module mux161 (
  input  [15:0] in_1,
  input  [7:0] in_2,
  input  [7:0] in_3,
  input  [7:0] in_4,
  input  [7:0] in_5,
  input  [7:0] in_6,
  input  [7:0] in_7,
  input  [7:0] in_8,
  input  [7:0] in_9,
  input  [7:0] in_10,
  input  [7:0] in_11,
  input  [7:0] in_12,
  input  [7:0] in_13,
  input  [7:0] in_14,
  input  [7:0] in_15,
  input  [7:0] in_16,
  input  [7:0] in_17,
  output [7:0] out_18
);

  mux161blk mux161blk_1 (
    .in_1(in_17[0]), .in_2(in_1[15]), .in_3(in_16[0]), .in_4(in_1[14]), .in_5(in_15[0]), .in_6(in_1[13]),
    .in_7(in_14[0]), .in_8(in_1[12]), .in_9(in_13[0]), .in_10(in_1[11]), .in_11(in_12[0]), .in_12(in_1[10]),
    .in_13(in_11[0]), .in_14(in_1[9]), .in_15(in_10[0]), .in_16(in_1[8]), .in_17(in_9[0]), .in_18(in_1[7]),
    .in_19(in_8[0]), .in_20(in_1[6]), .in_21(in_7[0]), .in_22(in_1[5]), .in_23(in_6[0]), .in_24(in_1[4]),
    .in_25(in_5[0]), .in_26(in_1[3]), .in_27(in_4[0]), .in_28(in_1[2]), .in_29(in_3[0]), .in_30(in_1[1]),
    .in_31(in_2[0]), .in_32(in_1[0]), .out_33(out_18[0]));
  mux161blk mux161blk_2 (
    .in_1(in_17[1]), .in_2(in_1[15]), .in_3(in_16[1]), .in_4(in_1[14]), .in_5(in_15[1]), .in_6(in_1[13]),
    .in_7(in_14[1]), .in_8(in_1[12]), .in_9(in_13[1]), .in_10(in_1[11]), .in_11(in_12[1]), .in_12(in_1[10]),
    .in_13(in_11[1]), .in_14(in_1[9]), .in_15(in_10[1]), .in_16(in_1[8]), .in_17(in_9[1]), .in_18(in_1[7]),
    .in_19(in_8[1]), .in_20(in_1[6]), .in_21(in_7[1]), .in_22(in_1[5]), .in_23(in_6[1]), .in_24(in_1[4]),
    .in_25(in_5[1]), .in_26(in_1[3]), .in_27(in_4[1]), .in_28(in_1[2]), .in_29(in_3[1]), .in_30(in_1[1]),
    .in_31(in_2[1]), .in_32(in_1[0]), .out_33(out_18[1]));
  mux161blk mux161blk_3 (
    .in_1(in_17[2]), .in_2(in_1[15]), .in_3(in_16[2]), .in_4(in_1[14]), .in_5(in_15[2]), .in_6(in_1[13]),
    .in_7(in_14[2]), .in_8(in_1[12]), .in_9(in_13[2]), .in_10(in_1[11]), .in_11(in_12[2]), .in_12(in_1[10]),
    .in_13(in_11[2]), .in_14(in_1[9]), .in_15(in_10[2]), .in_16(in_1[8]), .in_17(in_9[2]), .in_18(in_1[7]),
    .in_19(in_8[2]), .in_20(in_1[6]), .in_21(in_7[2]), .in_22(in_1[5]), .in_23(in_6[2]), .in_24(in_1[4]),
    .in_25(in_5[2]), .in_26(in_1[3]), .in_27(in_4[2]), .in_28(in_1[2]), .in_29(in_3[2]), .in_30(in_1[1]),
    .in_31(in_2[2]), .in_32(in_1[0]), .out_33(out_18[2]));
  mux161blk mux161blk_4 (
    .in_1(in_17[3]), .in_2(in_1[15]), .in_3(in_16[3]), .in_4(in_1[14]), .in_5(in_15[3]), .in_6(in_1[13]),
    .in_7(in_14[3]), .in_8(in_1[12]), .in_9(in_13[3]), .in_10(in_1[11]), .in_11(in_12[3]), .in_12(in_1[10]),
    .in_13(in_11[3]), .in_14(in_1[9]), .in_15(in_10[3]), .in_16(in_1[8]), .in_17(in_9[3]), .in_18(in_1[7]),
    .in_19(in_8[3]), .in_20(in_1[6]), .in_21(in_7[3]), .in_22(in_1[5]), .in_23(in_6[3]), .in_24(in_1[4]),
    .in_25(in_5[3]), .in_26(in_1[3]), .in_27(in_4[3]), .in_28(in_1[2]), .in_29(in_3[3]), .in_30(in_1[1]),
    .in_31(in_2[3]), .in_32(in_1[0]), .out_33(out_18[3]));
  mux161blk mux161blk_5 (
    .in_1(in_17[4]), .in_2(in_1[15]), .in_3(in_16[4]), .in_4(in_1[14]), .in_5(in_15[4]), .in_6(in_1[13]),
    .in_7(in_14[4]), .in_8(in_1[12]), .in_9(in_13[4]), .in_10(in_1[11]), .in_11(in_12[4]), .in_12(in_1[10]),
    .in_13(in_11[4]), .in_14(in_1[9]), .in_15(in_10[4]), .in_16(in_1[8]), .in_17(in_9[4]), .in_18(in_1[7]),
    .in_19(in_8[4]), .in_20(in_1[6]), .in_21(in_7[4]), .in_22(in_1[5]), .in_23(in_6[4]), .in_24(in_1[4]),
    .in_25(in_5[4]), .in_26(in_1[3]), .in_27(in_4[4]), .in_28(in_1[2]), .in_29(in_3[4]), .in_30(in_1[1]),
    .in_31(in_2[4]), .in_32(in_1[0]), .out_33(out_18[4]));
  mux161blk mux161blk_6 (
    .in_1(in_17[5]), .in_2(in_1[15]), .in_3(in_16[5]), .in_4(in_1[14]), .in_5(in_15[5]), .in_6(in_1[13]),
    .in_7(in_14[5]), .in_8(in_1[12]), .in_9(in_13[5]), .in_10(in_1[11]), .in_11(in_12[5]), .in_12(in_1[10]),
    .in_13(in_11[5]), .in_14(in_1[9]), .in_15(in_10[5]), .in_16(in_1[8]), .in_17(in_9[5]), .in_18(in_1[7]),
    .in_19(in_8[5]), .in_20(in_1[6]), .in_21(in_7[5]), .in_22(in_1[5]), .in_23(in_6[5]), .in_24(in_1[4]),
    .in_25(in_5[5]), .in_26(in_1[3]), .in_27(in_4[5]), .in_28(in_1[2]), .in_29(in_3[5]), .in_30(in_1[1]),
    .in_31(in_2[5]), .in_32(in_1[0]), .out_33(out_18[5]));
  mux161blk mux161blk_7 (
    .in_1(in_17[6]), .in_2(in_1[15]), .in_3(in_16[6]), .in_4(in_1[14]), .in_5(in_15[6]), .in_6(in_1[13]),
    .in_7(in_14[6]), .in_8(in_1[12]), .in_9(in_13[6]), .in_10(in_1[11]), .in_11(in_12[6]), .in_12(in_1[10]),
    .in_13(in_11[6]), .in_14(in_1[9]), .in_15(in_10[6]), .in_16(in_1[8]), .in_17(in_9[6]), .in_18(in_1[7]),
    .in_19(in_8[6]), .in_20(in_1[6]), .in_21(in_7[6]), .in_22(in_1[5]), .in_23(in_6[6]), .in_24(in_1[4]),
    .in_25(in_5[6]), .in_26(in_1[3]), .in_27(in_4[6]), .in_28(in_1[2]), .in_29(in_3[6]), .in_30(in_1[1]),
    .in_31(in_2[6]), .in_32(in_1[0]), .out_33(out_18[6]));
  mux161blk mux161blk_8 (
    .in_1(in_17[7]), .in_2(in_1[15]), .in_3(in_16[7]), .in_4(in_1[14]), .in_5(in_15[7]), .in_6(in_1[13]),
    .in_7(in_14[7]), .in_8(in_1[12]), .in_9(in_13[7]), .in_10(in_1[11]), .in_11(in_12[7]), .in_12(in_1[10]),
    .in_13(in_11[7]), .in_14(in_1[9]), .in_15(in_10[7]), .in_16(in_1[8]), .in_17(in_9[7]), .in_18(in_1[7]),
    .in_19(in_8[7]), .in_20(in_1[6]), .in_21(in_7[7]), .in_22(in_1[5]), .in_23(in_6[7]), .in_24(in_1[4]),
    .in_25(in_5[7]), .in_26(in_1[3]), .in_27(in_4[7]), .in_28(in_1[2]), .in_29(in_3[7]), .in_30(in_1[1]),
    .in_31(in_2[7]), .in_32(in_1[0]), .out_33(out_18[7]));
endmodule

module mux218 (
  input  in_1,
  input  in_2,
  input  in_3,
  input  in_4,
  input  in_5,
  input  in_6,
  input  in_7,
  input  in_8,
  input  in_9,
  input  in_10,
  input  in_11,
  input  in_12,
  input  in_13,
  input  in_14,
  input  in_15,
  input  in_16,
  input  in_17,
  output out_18,
  output out_19,
  output out_20,
  output out_21,
  output out_22,
  output out_23,
  output out_24,
  output out_25
);

  mux21 mux21_1 (.a0(in_1), .s(in_2), .a0_2(in_3), .y(out_18));
  mux21 mux21_2 (.a0(in_4), .s(in_2), .a0_2(in_5), .y(out_19));
  mux21 mux21_3 (.a0(in_6), .s(in_2), .a0_2(in_7), .y(out_20));
  mux21 mux21_4 (.a0(in_8), .s(in_2), .a0_2(in_9), .y(out_21));
  mux21 mux21_5 (.a0(in_10), .s(in_2), .a0_2(in_11), .y(out_22));
  mux21 mux21_6 (.a0(in_12), .s(in_2), .a0_2(in_13), .y(out_23));
  mux21 mux21_7 (.a0(in_14), .s(in_2), .a0_2(in_15), .y(out_24));
  mux21 mux21_8 (.a0(in_16), .s(in_2), .a0_2(in_17), .y(out_25));
endmodule

module opinterp (
  input  in_1,
  input  in_2,
  input  in_3,
  input  in_4,
  output out_5,
  output out_6,
  output out_7,
  output out_8,
  output out_9,
  output out_10,
  output out_11,
  output out_12
);

  wire and_1_out_3, and_2_out_3, and_3_out_3, and_4_out_3, and_5_out_3, and_6_out_3, and_7_out_3,
       and_8_out_3, and_9_out_3, and_10_out_3, and_11_out_3, and_12_out_3, and_13_out_3, and_14_out_3,
       and_15_out_3, and_16_out_3, nand_1_out, nand_2_out, nand_3_out;

  nand nand_1 (nand_1_out, in_1, in_1);
  nand nand_2 (nand_2_out, in_2, in_2);
  nand nand_3 (nand_3_out, in_3, in_3);
  \and  and_1 (.in_1(nand_1_out), .in_2(nand_2_out), .out_3(and_1_out_3));
  \and  and_2 (.in_1(nand_3_out), .in_2(in_4), .out_3(and_2_out_3));
  \and  and_3 (.in_1(in_1), .in_2(nand_2_out), .out_3(and_3_out_3));
  \and  and_4 (.in_1(nand_3_out), .in_2(in_4), .out_3(and_4_out_3));
  \and  and_5 (.in_1(nand_1_out), .in_2(in_2), .out_3(and_5_out_3));
  \and  and_6 (.in_1(nand_3_out), .in_2(in_4), .out_3(and_6_out_3));
  \and  and_7 (.in_1(in_1), .in_2(in_2), .out_3(and_7_out_3));
  \and  and_8 (.in_1(nand_3_out), .in_2(in_4), .out_3(and_8_out_3));
  \and  and_9 (.in_1(nand_1_out), .in_2(nand_2_out), .out_3(and_9_out_3));
  \and  and_10 (.in_1(in_3), .in_2(in_4), .out_3(and_10_out_3));
  \and  and_11 (.in_1(in_1), .in_2(nand_2_out), .out_3(and_11_out_3));
  \and  and_12 (.in_1(in_3), .in_2(in_4), .out_3(and_12_out_3));
  \and  and_13 (.in_1(nand_1_out), .in_2(in_2), .out_3(and_13_out_3));
  \and  and_14 (.in_1(in_3), .in_2(in_4), .out_3(and_14_out_3));
  \and  and_15 (.in_1(in_1), .in_2(in_2), .out_3(and_15_out_3));
  \and  and_16 (.in_1(in_3), .in_2(in_4), .out_3(and_16_out_3));
  \and  and_17 (.in_1(and_1_out_3), .in_2(and_2_out_3), .out_3(out_5));
  \and  and_18 (.in_1(and_3_out_3), .in_2(and_4_out_3), .out_3(out_6));
  \and  and_19 (.in_1(and_5_out_3), .in_2(and_6_out_3), .out_3(out_7));
  \and  and_20 (.in_1(and_7_out_3), .in_2(and_8_out_3), .out_3(out_8));
  \and  and_21 (.in_1(and_9_out_3), .in_2(and_10_out_3), .out_3(out_9));
  \and  and_22 (.in_1(and_11_out_3), .in_2(and_12_out_3), .out_3(out_10));
  \and  and_23 (.in_1(and_13_out_3), .in_2(and_14_out_3), .out_3(out_11));
  \and  and_24 (.in_1(and_15_out_3), .in_2(and_16_out_3), .out_3(out_12));
endmodule

module mux51blk (
  input  in_1,
  input  in_2,
  input  in_3,
  input  in_4,
  input  in_5,
  input  in_6,
  input  in_7,
  input  in_8,
  input  in_9,
  input  in_10,
  output out_11
);

  wire and_1_out_3, and_2_out_3, and_3_out_3, nand_1_out, nand_2_out, nand_3_out, nand_4_out, nand_5_out;

  nand nand_1 (nand_1_out, in_1, in_2);
  nand nand_2 (nand_2_out, in_3, in_4);
  nand nand_3 (nand_3_out, in_5, in_6);
  nand nand_4 (nand_4_out, in_7, in_8);
  nand nand_5 (nand_5_out, in_9, in_10);
  \and  and_1 (.in_1(nand_1_out), .in_2(nand_2_out), .out_3(and_1_out_3));
  \and  and_2 (.in_1(nand_3_out), .in_2(nand_4_out), .out_3(and_2_out_3));
  \and  and_3 (.in_1(and_1_out_3), .in_2(and_2_out_3), .out_3(and_3_out_3));
  nand nand_6 (out_11, and_3_out_3, nand_5_out);
endmodule

module mux51 (
  input  [7:0] in_1,
  input  [7:0] in_2,
  input  [7:0] in_3,
  input  [7:0] in_4,
  input  [7:0] in_5,
  input  in_6,
  input  in_7,
  input  in_8,
  input  in_9,
  input  in_10,
  output [7:0] out_11
);

  mux51blk mux51blk_1 (
    .in_1(in_10), .in_2(in_5[7]), .in_3(in_9), .in_4(in_4[0]), .in_5(in_8), .in_6(in_3[0]), .in_7(in_7),
    .in_8(in_2[0]), .in_9(in_6), .in_10(in_1[0]), .out_11(out_11[0]));
  mux51blk mux51blk_2 (
    .in_1(in_10), .in_2(in_5[6]), .in_3(in_9), .in_4(in_4[1]), .in_5(in_8), .in_6(in_3[1]), .in_7(in_7),
    .in_8(in_2[1]), .in_9(in_6), .in_10(in_1[1]), .out_11(out_11[1]));
  mux51blk mux51blk_3 (
    .in_1(in_10), .in_2(in_5[5]), .in_3(in_9), .in_4(in_4[2]), .in_5(in_8), .in_6(in_3[2]), .in_7(in_7),
    .in_8(in_2[2]), .in_9(in_6), .in_10(in_1[2]), .out_11(out_11[2]));
  mux51blk mux51blk_4 (
    .in_1(in_10), .in_2(in_5[4]), .in_3(in_9), .in_4(in_4[3]), .in_5(in_8), .in_6(in_3[3]), .in_7(in_7),
    .in_8(in_2[3]), .in_9(in_6), .in_10(in_1[3]), .out_11(out_11[3]));
  mux51blk mux51blk_5 (
    .in_1(in_10), .in_2(in_5[3]), .in_3(in_9), .in_4(in_4[4]), .in_5(in_8), .in_6(in_3[4]), .in_7(in_7),
    .in_8(in_2[4]), .in_9(in_6), .in_10(in_1[4]), .out_11(out_11[4]));
  mux51blk mux51blk_6 (
    .in_1(in_10), .in_2(in_5[2]), .in_3(in_9), .in_4(in_4[5]), .in_5(in_8), .in_6(in_3[5]), .in_7(in_7),
    .in_8(in_2[5]), .in_9(in_6), .in_10(in_1[5]), .out_11(out_11[5]));
  mux51blk mux51blk_7 (
    .in_1(in_10), .in_2(in_5[1]), .in_3(in_9), .in_4(in_4[6]), .in_5(in_8), .in_6(in_3[6]), .in_7(in_7),
    .in_8(in_2[6]), .in_9(in_6), .in_10(in_1[6]), .out_11(out_11[6]));
  mux51blk mux51blk_8 (
    .in_1(in_10), .in_2(in_5[0]), .in_3(in_9), .in_4(in_4[7]), .in_5(in_8), .in_6(in_3[7]), .in_7(in_7),
    .in_8(in_2[7]), .in_9(in_6), .in_10(in_1[7]), .out_11(out_11[7]));
endmodule

module _16add (
  input  b7,
  input  b6,
  input  b5,
  input  b4,
  input  b3,
  input  b2,
  input  b1,
  input  b0,
  input  b7_2,
  input  b6_2,
  input  b5_2,
  input  b4_2,
  input  b3_2,
  input  b2_2,
  input  b1_2,
  input  b0_2,
  input  a7,
  input  a6,
  input  a5,
  input  a4,
  input  a3,
  input  a2,
  input  a1,
  input  a0,
  input  a7_2,
  input  a6_2,
  input  a5_2,
  input  a4_2,
  input  a3_2,
  input  a2_2,
  input  a1_2,
  input  a0_2,
  output s7,
  output s6,
  output s5,
  output s4,
  output s3,
  output s2,
  output s1,
  output s0,
  output s7_2,
  output s6_2,
  output s5_2,
  output s4_2,
  output s3_2,
  output s2_2,
  output s1_2,
  output s0_2
);

  wire clu16_1_c1, clu16_1_c1_2, clu16_1_c2, clu16_1_c2_2, clu16_1_c3, clu16_1_c3_2, clu16_1_c4,
       clu16_1_c4_2, clu16_1_c5, clu16_1_c5_2, clu16_1_c6, clu16_1_c6_2, clu16_1_c7, clu16_1_c7_2,
       clu16_1_c8, pfa_1_g_n, pfa_1_p, pfa_2_g_n, pfa_2_p, pfa_3_g_n, pfa_3_p, pfa_4_g_n, pfa_4_p, pfa_5_g_n,
       pfa_5_p, pfa_6_g_n, pfa_6_p, pfa_7_g_n, pfa_7_p, pfa_8_g_n, pfa_8_p, pfa_9_g_n, pfa_9_p, pfa_10_g_n,
       pfa_10_p, pfa_11_g_n, pfa_11_p, pfa_12_g_n, pfa_12_p, pfa_13_g_n, pfa_13_p, pfa_14_g_n, pfa_14_p,
       pfa_15_g_n, pfa_15_p, pfa_16_g_n, pfa_16_p;

  pfa pfa_1 (.a(a7), .b(b7), .c(clu16_1_c7_2), .g_n(pfa_1_g_n), .s(s7), .p(pfa_1_p));
  pfa pfa_2 (.a(a6), .b(b6), .c(clu16_1_c6_2), .g_n(pfa_2_g_n), .s(s6), .p(pfa_2_p));
  pfa pfa_3 (.a(a5), .b(b5), .c(clu16_1_c5_2), .g_n(pfa_3_g_n), .s(s5), .p(pfa_3_p));
  pfa pfa_4 (.a(a4), .b(b4), .c(clu16_1_c4_2), .g_n(pfa_4_g_n), .s(s4), .p(pfa_4_p));
  pfa pfa_5 (.a(a3), .b(b3), .c(clu16_1_c3_2), .g_n(pfa_5_g_n), .s(s3), .p(pfa_5_p));
  pfa pfa_6 (.a(a2), .b(b2), .c(clu16_1_c2_2), .g_n(pfa_6_g_n), .s(s2), .p(pfa_6_p));
  pfa pfa_7 (.a(a1), .b(b1), .c(clu16_1_c1_2), .g_n(pfa_7_g_n), .s(s1), .p(pfa_7_p));
  pfa pfa_8 (.a(a0), .b(b0), .c(clu16_1_c8), .g_n(pfa_8_g_n), .s(s0), .p(pfa_8_p));
  pfa pfa_9 (.a(a7_2), .b(b7_2), .c(clu16_1_c7), .g_n(pfa_9_g_n), .s(s7_2), .p(pfa_9_p));
  pfa pfa_10 (.a(a6_2), .b(b6_2), .c(clu16_1_c6), .g_n(pfa_10_g_n), .s(s6_2), .p(pfa_10_p));
  pfa pfa_11 (.a(a5_2), .b(b5_2), .c(clu16_1_c5), .g_n(pfa_11_g_n), .s(s5_2), .p(pfa_11_p));
  clu16 clu16_1 (
    .c0(1'b0), .p0(pfa_16_p), .g_n0(pfa_16_g_n), .p1(pfa_15_p), .g_n1(pfa_15_g_n), .p2(pfa_14_p),
    .g_n2(pfa_14_g_n), .p3(pfa_13_p), .g_n3(pfa_13_g_n), .p4(pfa_12_p), .g_n4(pfa_12_g_n), .p5(pfa_11_p),
    .g_n5(pfa_11_g_n), .p6(pfa_10_p), .g_n6(pfa_10_g_n), .p7(pfa_9_p), .g_n7(pfa_9_g_n), .p0_2(pfa_8_p),
    .g_n0_2(pfa_8_g_n), .p1_2(pfa_7_p), .g_n1_2(pfa_7_g_n), .p2_2(pfa_6_p), .g_n2_2(pfa_6_g_n),
    .p3_2(pfa_5_p), .g_n3_2(pfa_5_g_n), .p4_2(pfa_4_p), .g_n4_2(pfa_4_g_n), .p5_2(pfa_3_p),
    .g_n5_2(pfa_3_g_n), .p6_2(pfa_2_p), .g_n6_2(pfa_2_g_n), .p7_2(pfa_1_p), .g_n7_2(pfa_1_g_n),
    .c1(clu16_1_c1), .c2(clu16_1_c2), .c3(clu16_1_c3), .c4(clu16_1_c4), .c5(clu16_1_c5), .c6(clu16_1_c6),
    .c7(clu16_1_c7), .c8(clu16_1_c8), .c1_2(clu16_1_c1_2), .c2_2(clu16_1_c2_2), .c3_2(clu16_1_c3_2),
    .c4_2(clu16_1_c4_2), .c5_2(clu16_1_c5_2), .c6_2(clu16_1_c6_2), .c7_2(clu16_1_c7_2));  // open: c8_2
  pfa pfa_12 (.a(a4_2), .b(b4_2), .c(clu16_1_c4), .g_n(pfa_12_g_n), .s(s4_2), .p(pfa_12_p));
  pfa pfa_13 (.a(a3_2), .b(b3_2), .c(clu16_1_c3), .g_n(pfa_13_g_n), .s(s3_2), .p(pfa_13_p));
  pfa pfa_14 (.a(a2_2), .b(b2_2), .c(clu16_1_c2), .g_n(pfa_14_g_n), .s(s2_2), .p(pfa_14_p));
  pfa pfa_15 (.a(a1_2), .b(b1_2), .c(clu16_1_c1), .g_n(pfa_15_g_n), .s(s1_2), .p(pfa_15_p));
  pfa pfa_16 (.a(a0_2), .b(b0_2), .c(1'b0), .g_n(pfa_16_g_n), .s(s0_2), .p(pfa_16_p));
endmodule

module clu16 (
  input  c0,
  input  p0,
  input  g_n0,
  input  p1,
  input  g_n1,
  input  p2,
  input  g_n2,
  input  p3,
  input  g_n3,
  input  p4,
  input  g_n4,
  input  p5,
  input  g_n5,
  input  p6,
  input  g_n6,
  input  p7,
  input  g_n7,
  input  p0_2,
  input  g_n0_2,
  input  p1_2,
  input  g_n1_2,
  input  p2_2,
  input  g_n2_2,
  input  p3_2,
  input  g_n3_2,
  input  p4_2,
  input  g_n4_2,
  input  p5_2,
  input  g_n5_2,
  input  p6_2,
  input  g_n6_2,
  input  p7_2,
  input  g_n7_2,
  output c1,
  output c2,
  output c3,
  output c4,
  output c5,
  output c6,
  output c7,
  output c8,
  output c1_2,
  output c2_2,
  output c3_2,
  output c4_2,
  output c5_2,
  output c6_2,
  output c7_2,
  output c8_2
);

  clublk clublk_1 (.in_1(c0), .in_2(p0), .in_3(g_n0), .out_4(c1));
  clublk clublk_2 (.in_1(c8), .in_2(p0_2), .in_3(g_n0_2), .out_4(c1_2));
  clublk clublk_3 (.in_1(c1), .in_2(p1), .in_3(g_n1), .out_4(c2));
  clublk clublk_4 (.in_1(c1_2), .in_2(p1_2), .in_3(g_n1_2), .out_4(c2_2));
  clublk clublk_5 (.in_1(c2), .in_2(p2), .in_3(g_n2), .out_4(c3));
  clublk clublk_6 (.in_1(c2_2), .in_2(p2_2), .in_3(g_n2_2), .out_4(c3_2));
  clublk clublk_7 (.in_1(c3), .in_2(p3), .in_3(g_n3), .out_4(c4));
  clublk clublk_8 (.in_1(c3_2), .in_2(p3_2), .in_3(g_n3_2), .out_4(c4_2));
  clublk clublk_9 (.in_1(c4), .in_2(p4), .in_3(g_n4), .out_4(c5));
  clublk clublk_10 (.in_1(c4_2), .in_2(p4_2), .in_3(g_n4_2), .out_4(c5_2));
  clublk clublk_11 (.in_1(c5), .in_2(p5), .in_3(g_n5), .out_4(c6));
  clublk clublk_12 (.in_1(c5_2), .in_2(p5_2), .in_3(g_n5_2), .out_4(c6_2));
  clublk clublk_13 (.in_1(c6), .in_2(p6), .in_3(g_n6), .out_4(c7));
  clublk clublk_14 (.in_1(c6_2), .in_2(p6_2), .in_3(g_n6_2), .out_4(c7_2));
  clublk clublk_15 (.in_1(c7), .in_2(p7), .in_3(g_n7), .out_4(c8));
  clublk clublk_16 (.in_1(c7_2), .in_2(p7_2), .in_3(g_n7_2), .out_4(c8_2));
endmodule

module mux2116 (
  input  in_1,
  input  in_2,
  input  in_3,
  input  in_4,
  input  in_5,
  input  in_6,
  input  in_7,
  input  in_8,
  input  in_9,
  input  in_10,
  input  in_11,
  input  in_12,
  input  in_13,
  input  in_14,
  input  in_15,
  input  in_16,
  input  in_17,
  input  in_18,
  input  in_19,
  input  in_20,
  input  in_21,
  input  in_22,
  input  in_23,
  input  in_24,
  input  in_25,
  input  in_26,
  input  in_27,
  input  in_28,
  input  in_29,
  input  in_30,
  input  in_31,
  input  in_32,
  input  in_33,
  output out_34,
  output out_35,
  output out_36,
  output out_37,
  output out_38,
  output out_39,
  output out_40,
  output out_41,
  output out_42,
  output out_43,
  output out_44,
  output out_45,
  output out_46,
  output out_47,
  output out_48,
  output out_49
);

  mux21 mux21_1 (.a0(in_1), .s(in_2), .a0_2(in_3), .y(out_34));
  mux21 mux21_2 (.a0(in_4), .s(in_2), .a0_2(in_5), .y(out_35));
  mux21 mux21_3 (.a0(in_6), .s(in_2), .a0_2(in_7), .y(out_36));
  mux21 mux21_4 (.a0(in_8), .s(in_2), .a0_2(in_9), .y(out_37));
  mux21 mux21_5 (.a0(in_10), .s(in_2), .a0_2(in_11), .y(out_38));
  mux21 mux21_6 (.a0(in_12), .s(in_2), .a0_2(in_13), .y(out_39));
  mux21 mux21_7 (.a0(in_14), .s(in_2), .a0_2(in_15), .y(out_40));
  mux21 mux21_8 (.a0(in_16), .s(in_2), .a0_2(in_17), .y(out_41));
  mux21 mux21_9 (.a0(in_18), .s(in_2), .a0_2(in_19), .y(out_42));
  mux21 mux21_10 (.a0(in_20), .s(in_2), .a0_2(in_21), .y(out_43));
  mux21 mux21_11 (.a0(in_22), .s(in_2), .a0_2(in_23), .y(out_44));
  mux21 mux21_12 (.a0(in_24), .s(in_2), .a0_2(in_25), .y(out_45));
  mux21 mux21_13 (.a0(in_26), .s(in_2), .a0_2(in_27), .y(out_46));
  mux21 mux21_14 (.a0(in_28), .s(in_2), .a0_2(in_29), .y(out_47));
  mux21 mux21_15 (.a0(in_30), .s(in_2), .a0_2(in_31), .y(out_48));
  mux21 mux21_16 (.a0(in_32), .s(in_2), .a0_2(in_33), .y(out_49));
endmodule

module equality (
  input  in_1,
  input  in_2,
  input  in_3,
  input  in_4,
  input  in_5,
  input  in_6,
  output out_7
);

  wire and3_1_out_4, and3_2_out_4, and3_3_out_4, and3_4_out_4, and3_5_out_4, and3_6_out_4, and_1_out_3,
       and_2_out_3, and_3_out_3, and_4_out_3, and_5_out_3, and_6_out_3, and_7_out_3, and_8_out_3,
       and_9_out_3, and_10_out_3, and_11_out_3, and_12_out_3, and_13_out_3, and_14_out_3, and_15_out_3,
       nand_1_out, nand_2_out, nand_3_out, nand_4_out, not_1_out_2, not_2_out_2, not_3_out_2, not_4_out_2,
       or_1_out_3, or_2_out_3, or_3_out_3, or_4_out_3, or_5_out_3;

  nand nand_1 (nand_1_out, in_1, in_1);
  nand nand_2 (nand_2_out, in_2, in_2);
  nand nand_3 (nand_3_out, nand_1_out, nand_2_out);
  nand nand_4 (nand_4_out, nand_3_out, nand_3_out);
  \not  not_1 (.in_1(in_3), .out_2(not_1_out_2));
  \not  not_2 (.in_1(in_4), .out_2(not_2_out_2));
  \not  not_3 (.in_1(in_5), .out_2(not_3_out_2));
  \not  not_4 (.in_1(in_6), .out_2(not_4_out_2));
  \and  and_1 (.in_1(in_2), .in_2(in_3), .out_3(and_1_out_3));
  and3 and3_1 (.in_1(not_2_out_2), .in_2(not_3_out_2), .in_3(not_4_out_2), .out_4(and3_1_out_4));
  and3 and3_2 (.in_1(in_4), .in_2(not_3_out_2), .in_3(not_4_out_2), .out_4(and3_2_out_4));
  and3 and3_3 (.in_1(in_4), .in_2(not_4_out_2), .in_3(not_1_out_2), .out_4(and3_3_out_4));
  and3 and3_4 (.in_1(not_3_out_2), .in_2(in_5), .in_3(not_4_out_2), .out_4(and3_4_out_4));
  and3 and3_5 (.in_1(not_2_out_2), .in_2(in_5), .in_3(not_4_out_2), .out_4(and3_5_out_4));
  and3 and3_6 (.in_1(in_4), .in_2(in_5), .in_3(not_4_out_2), .out_4(and3_6_out_4));
  \and  and_2 (.in_1(nand_4_out), .in_2(not_1_out_2), .out_3(and_2_out_3));
  \and  and_3 (.in_1(nand_1_out), .in_2(in_3), .out_3(and_3_out_3));
  \and  and_4 (.in_1(in_1), .in_2(not_1_out_2), .out_3(and_4_out_3));
  \and  and_5 (.in_1(nand_3_out), .in_2(in_3), .out_3(and_5_out_3));
  \and  and_6 (.in_1(nand_2_out), .in_2(not_1_out_2), .out_3(and_6_out_3));
  \and  and_7 (.in_1(not_1_out_2), .in_2(not_2_out_2), .out_3(and_7_out_3));
  \and  and_8 (.in_1(not_3_out_2), .in_2(not_4_out_2), .out_3(and_8_out_3));
  \and  and_9 (.in_1(and_1_out_3), .in_2(and3_1_out_4), .out_3(and_9_out_3));
  \and  and_10 (.in_1(and_2_out_3), .in_2(and3_2_out_4), .out_3(and_10_out_3));
  \and  and_11 (.in_1(and_3_out_3), .in_2(and3_3_out_4), .out_3(and_11_out_3));
  \and  and_12 (.in_1(and_4_out_3), .in_2(and3_4_out_4), .out_3(and_12_out_3));
  \and  and_13 (.in_1(and_5_out_3), .in_2(and3_5_out_4), .out_3(and_13_out_3));
  \and  and_14 (.in_1(and_6_out_3), .in_2(and3_6_out_4), .out_3(and_14_out_3));
  \and  and_15 (.in_1(and_7_out_3), .in_2(and_8_out_3), .out_3(and_15_out_3));
  \or  or_1 (.in_1(and_9_out_3), .in_2(and_10_out_3), .out_3(or_1_out_3));
  \or  or_2 (.in_1(and_11_out_3), .in_2(and_12_out_3), .out_3(or_2_out_3));
  \or  or_3 (.in_1(and_13_out_3), .in_2(and_14_out_3), .out_3(or_3_out_3));
  \or  or_4 (.in_1(or_1_out_3), .in_2(or_2_out_3), .out_3(or_4_out_3));
  \or  or_5 (.in_1(or_3_out_3), .in_2(and_15_out_3), .out_3(or_5_out_3));
  \or  or_6 (.in_1(or_4_out_3), .in_2(or_5_out_3), .out_3(out_7));
endmodule
